// Logisim project Single-Cycle-and-Pipelined-MIPS-Processor.circ as structural Verilog: 54 circuits, main circuit Main
module Main (
  input  in_1,
  input  in_2,
  input  in_3,
  input  in_4,
  output over_flow
);

  wire alu_src, alu_src_1, and_1_out, and_2_out, and_3_out, beq, beqz, bgez, blez, bltz, bne, bnez, bqtz,
       Branch, Branch_1, c_in, c_in_1, clock, comparator_2_eq, comparator_3_eq, d_ff_1_q, en, en_1, Flush_ID,
       Flush_IF, Flush_Select, Forward_E, Forward_G, Forward_H, Hold_PC, Imm_In, Imm_In_1, Mem_Read_1,
       Mem_Read_2, Mem_Write_1, Mem_Write_2, No_Op, not_1_out, not_2_out, not_3_out, not_4_out, not_5_out,
       or_1_out, re_write_1, re_write_2, re_write_3, Rs__in, Rt____RD_1, Rt_in, Set___Sset_1;
  wire [1:0] Forward_A, Forward_B, Forward_C, Forward_D, \function , Imm_Selct, Imm_Selct_1, Mem_to_reg_1,
       Mem_to_reg_2, Mem_to_reg_3, red___dest_1, shift_selector_1;
  wire [2:0] multiplexer_2_out, Rd, Rd_1, Rd_2, Rd_3, Rs_1, Rt0, Rt_1;
  wire [3:0] alu_op, alu_op_1, Pc_Next_1;
  wire [4:0] Imm_5__EX, opcode, opcode_1;
  wire [4:2] Imm_5;
  wire [7:0] Imm_8_1;
  wire [7:5] Imm_8;
  wire [10:8] Imm_11;
  wire [15:0] ram_1_data;
  wire [19:0] adder_3_out, bit_extender_1_out, bit_extender_2_out, bit_extender_3_out, bit_extender_4_out,
       if_detect, J_JAL, JR_JALR, multiplexer_1_out, PC, PC1, Pc_In, Pc_In_t, Pc_Out, shifter_1_out,
       shifter_2_out, shifter_3_out;
  wire [23:5] main_control;
  wire [25:0] multiplexer_9_out;
  wire [31:0] ALu_Output, ALu_Output0, bit_extender_6_out, bit_extender_7_out, Bus_B_data, data_input,
       Data_Mem_Output, Hazard_Out, mem_wb_1_alu_out_wb, mem_wb_1_memory_data_wb, multiplexer_3_out,
       multiplexer_4_out, multiplexer_7_out, multiplexer_8_out, multiplexer_10_out, multiplexer_11_out,
       multiplexer_12_out, multiplexer_13_out, multiplexer_15_out, \output , Pc_2, Pc_2_1, Pc_2_2, Pc_2_3,
       Rd_data, Rd_data_2, Rd_data_3, reg_file_1_rd_2, reg_file_1_rs, Rs_data, Rt_data,
       wb_operation_detect_1_rs_2, wb_operation_detect_1_rt_2;

  not not_1 (not_1_out, Hold_PC);
  Register #(.width(20)) u_Pc (.D(Pc_Out), .en(not_1_out), .Q(if_detect), .clk(clock), .clr(in_4));
  Clock u_clock (.out(clock));
  assign bit_extender_1_out = {{15{Imm_5[4]}}, {Imm_5, \function }};  // Bit_Extender bit_extender_1
  assign bit_extender_2_out = {{12{Imm_8[7]}}, {Imm_8, Imm_5, \function }};  // Bit_Extender bit_extender_2
  Adder #(.width(20)) adder_1 (.a(shifter_1_out), .b(PC), .out(Pc_In));  // open: cin, cout
  Multiplexer #(.width(20)) multiplexer_1 (
    .in0(bit_extender_1_out), .in1(bit_extender_2_out), .out(multiplexer_1_out), .sel(Imm_In));  // open: en
  Shifter #(.width(20)) shifter_1 (.in(multiplexer_1_out), .\dist (5'b00001), .out(shifter_1_out));
  RAM #(.addrWidth(19), .dataWidth(16)) ram_1 (
    .addr(if_detect[18:0]), .data(ram_1_data), .sel(1'b1), .clk(clock), .ld(1'b1), .clr(in_1));
  D_Flip_Flop d_ff_1 (.clk(clock), .D(No_Op), .Q(d_ff_1_q));  // open: Qn, preset, en, reset
  IF_ID if_id_1 (
    .Next_Pc_ID(if_detect), .Instruction_ID(ram_1_data), .Next_Pc_IF(PC),
    .Instruction_IF({opcode, Imm_11, Imm_8, Imm_5, \function }), .CLK(clock), .en(not_2_out),
    .Clear(and_1_out));
  not not_2 (not_2_out, Flush_IF);
  and and_1 (and_1_out, d_ff_1_q, No_Op);
  PC u_pc_2 (
    .pc(PC), .\input (if_detect), .immediate(shifter_1_out), .J___JAL(J_JAL), .JALR(JR_JALR),
    .\output (Pc_Out), .in_11(main_control[16:13]), .branch(Branch), .beq(beq), .bnq(bne), .beqz(beqz),
    .bnez(bnez), .bltz(bltz), .bgeZ(bgez), .bgtz(bqtz), .blez(blez), .JR(JR_JALR));
  not not_3 (not_3_out, opcode[3]);
  Comparator comparator_1 (
    .RS_DATA(multiplexer_4_out), .RD_DATA(multiplexer_3_out), .Bne(bne), .Beq(beq), .BNEZ(bnez), .BEQZ(beqz),
    .BQTZ(bqtz), .BLTZ(bltz), .BGEZ(bgez), .BLEZ(blez));
  not not_4 (not_4_out, opcode[1]);
  not not_5 (not_5_out, opcode[2]);
  and and_2 (and_2_out, opcode[4], not_3_out, not_5_out, not_4_out, opcode[0]);
  Multiplexer #(.width(3)) multiplexer_2 (.in0(Rd_3), .in1(Rd), .out(multiplexer_2_out), .sel(and_2_out));  // open: en
  // Probe on \output 
  Multiplexer #(.width(32)) multiplexer_3 (
    .in0(multiplexer_7_out), .in1(Hazard_Out), .out(multiplexer_3_out), .sel(Forward_H));  // open: en
  Multiplexer #(.width(32)) multiplexer_4 (
    .in0(multiplexer_8_out), .in1(Hazard_Out), .out(multiplexer_4_out), .sel(Forward_G));  // open: en
  assign bit_extender_3_out = {{12{Imm_8[7]}}, {Imm_8, Imm_5, \function }};  // Bit_Extender bit_extender_3
  Multiplexer #(.select(2), .width(3)) multiplexer_5 (
    .in0(Imm_11), .in1(Imm_11), .in2(3'b111), .out(Rd), .sel(main_control[6:5]));  // open: in3, en
  Multiplexer #(.width(3)) multiplexer_6 (.in0(Imm_5), .in1(Imm_11), .out(Rt0), .sel(main_control[21]));  // open: en
  Shifter #(.width(20)) shifter_2 (.in(bit_extender_3_out), .\dist (5'b00001), .out(shifter_2_out));
  Adder #(.width(20)) adder_2 (.a(shifter_2_out), .b(data_input[19:0]), .out(JR_JALR));  // open: cin, cout
  Multiplexer #(.select(2), .width(32)) multiplexer_7 (
    .in0(reg_file_1_rs), .in1(ALu_Output), .in2(ALu_Output0), .out(multiplexer_7_out), .sel(Forward_D));  // open: in3, en
  Multiplexer #(.select(2), .width(32)) multiplexer_8 (
    .in0(data_input), .in1(ALu_Output), .in2(ALu_Output0), .out(multiplexer_8_out), .sel(Forward_C));  // open: in3, en
  Reg_File reg_file_1 (
    .Rd(multiplexer_2_out), .Ra(Imm_8), .Rb(Rt0), .Bus_W(\output ), .Rs(reg_file_1_rs), .Rt(data_input),
    .RD_2(reg_file_1_rd_2), .read_write(re_write_3), .clock(clock), .in_6(in_2));
  assign bit_extender_4_out = {{9{Imm_11[10]}}, {Imm_11, Imm_8, Imm_5, \function }};  // Bit_Extender bit_extender_4
  Multiplexer #(.width(26)) multiplexer_9 (
    .in0({Imm_Selct, main_control[23], Imm_In, main_control[21:19], c_in, Branch, main_control[16:9], alu_src, main_control[7:5], en, alu_op}),
    .in1({26{1'b0}}), .out(multiplexer_9_out), .sel(Flush_Select));  // open: en
  WB_OPeration_detect wb_operation_detect_1 (
    .RS(reg_file_1_rs), .RT(data_input), .WB_OUT(\output ), .H(Rs__in), .L(Rt_in),
    .RS_2(wb_operation_detect_1_rs_2), .RT_2(wb_operation_detect_1_rt_2));
  Adder #(.width(20)) adder_3 (.a(PC), .b(20'h2), .out(adder_3_out));  // open: cin, cout
  Shifter #(.width(20)) shifter_3 (.in(bit_extender_4_out), .\dist (5'b00001), .out(shifter_3_out));
  ID_EX id_ex_1 (
    .Control_ID(multiplexer_9_out), .PC_Next_ID(PC), ._5_bit_Imm_ID({Imm_5, \function }),
    .Bus_A_ID(wb_operation_detect_1_rs_2), .Bus_B_ID(wb_operation_detect_1_rt_2), .alu_op_1(alu_op_1),
    .en_1(en_1), .regdest_1(red___dest_1), .re_wr_1(re_write_1), .alu_src_1(alu_src_1),
    .mem_write_1(Mem_Write_1), .mem_read_1(Mem_Read_1), .mem_to_reg_1(Mem_to_reg_1), .pc_next_1(Pc_Next_1),
    .branch_1(Branch_1), .c_in_1(c_in_1), .shift_select_1(shift_selector_1), .rt___rd_1(Rt____RD_1),
    .imm_in_1(Imm_In_1), .set___sset_1(Set___Sset_1), .imm_selctor_1(Imm_Selct_1), .PC_Next_Ex(PC1),
    ._5_bit_Imm_EX(Imm_5__EX), .Bus_A_EX(Rs_data), .Bus_B_EX(Rt_data), .RT_ID(Imm_5), .RT_Ex(Rt_1),
    .RS_ID(Imm_8), .RS_EX(Rs_1), .RD_ID(Rd), .RD_EX(Rd_1), .CLK(clock), .Bus_D_ID(reg_file_1_rd_2),
    .Bus_D_EX(Rd_data), ._8_Imm({Imm_8, Imm_5, \function }), ._8_Imm_2(Imm_8_1), .in_14(Flush_ID),
    .PC_2(Pc_2), .PC_2_2(Pc_2_1), .Opcode_ID_Ex(opcode), .Opcode_EX_MEM(opcode_1));
  assign Pc_2 = {{12{adder_3_out[19]}}, adder_3_out};  // Bit_Extender bit_extender_5
  Adder #(.width(20)) adder_4 (.a(shifter_3_out), .b(PC), .out(J_JAL));  // open: cin, cout
  Comparator_part #(.width(3)) comparator_2 (.a(Rt_1), .b(Rd_2), .eq(comparator_2_eq));  // open: gt, lt
  Comparator_part #(.width(3)) comparator_3 (.a(Rs_1), .b(Rd_2), .eq(comparator_3_eq));  // open: gt, lt
  Multiplexer #(.width(32)) multiplexer_10 (
    .in0(ALu_Output), .in1(Data_Mem_Output), .out(multiplexer_10_out), .sel(and_3_out));  // open: en
  and and_3 (and_3_out, Mem_Read_2, or_1_out);
  or or_1 (or_1_out, comparator_2_eq, comparator_3_eq);
  Multiplexer #(.select(2), .width(32)) multiplexer_11 (
    .in0(Rs_data), .in1(\output ), .in2(ALu_Output), .out(multiplexer_11_out), .sel(Forward_A));  // open: in3, en
  Multiplexer #(.select(2), .width(32)) multiplexer_12 (
    .in0(Rt_data), .in1(\output ), .in2(multiplexer_10_out), .out(multiplexer_12_out), .sel(Forward_B));  // open: in3, en
  assign bit_extender_6_out = {{27{1'b0}}, Imm_5__EX};  // Bit_Extender bit_extender_6
  assign bit_extender_7_out = {{27{Imm_5__EX[4]}}, Imm_5__EX};  // Bit_Extender bit_extender_7
  // Probe on multiplexer_11_out
  Multiplexer #(.select(2), .width(32)) multiplexer_13 (
    .in0(bit_extender_6_out), .in1(bit_extender_7_out), .in2(bit_extender_7_out), .out(multiplexer_13_out),
    .sel(Imm_Selct_1));  // open: in3, en
  ALU alu_1 (
    .alu_out(ALu_Output0), .RS(multiplexer_11_out), .ALU_Selector(alu_op_1), .out_9(over_flow),
    .RT_DATA(Bus_B_data), .Imm_5(Imm_5__EX), .shift_selector(shift_selector_1), .cin(c_in_1), .Imm_8(Imm_8_1));
  Control_Unit control_unit_1 (
    .\function (\function ), .alu_op(alu_op), .en(en), .regdest(main_control[6:5]), .re_wr(main_control[7]),
    .alu_src(alu_src), .mem_write(main_control[9]), .mem_read(main_control[10]),
    .mem_to_reg(main_control[12:11]), .pc_next(main_control[16:13]), .branch(Branch), .c_in(c_in),
    .shift_select(main_control[20:19]), .rt__rd(main_control[21]), .imm_in(Imm_In),
    .set__sset(main_control[23]), .imm_selector(Imm_Selct), .Op_Code(opcode));
  Multiplexer #(.width(32)) multiplexer_14 (
    .in0(multiplexer_12_out), .in1(multiplexer_13_out), .out(Bus_B_data), .sel(alu_src_1));  // open: en
  // Probe on ALu_Output0
  Multiplexer #(.width(32)) multiplexer_15 (
    .in0(Rd_data), .in1(\output ), .out(multiplexer_15_out), .sel(Forward_E));  // open: en
  EX_MEM ex_mem_1 (
    .ALU_EX(ALu_Output0), .Memory_Data_EX(multiplexer_15_out), .RD_EX(Rd_1), .ALU_MEM(ALu_Output),
    .Memory_Data_MEM(Rd_data_2), .RD_MEM(Rd_2), .CLK(clock), .re_write1(re_write_1), .re_write_2(re_write_2),
    .Mem_Write_1(Mem_Write_1), .Mem_Write_2(Mem_Write_2), .Mem_Read_1(Mem_Read_1), .Mem_Read_2(Mem_Read_2),
    .Mem_to_reg_1(Mem_to_reg_1), .Mem_to_reg_1_2(Mem_to_reg_2), .PC_2(Pc_2_1), .PC_2_2(Pc_2_2));
  Main_Hazard_Unit main_hazard_unit_1 (
    .Clk(clock), .Rd_Ex___MEM(Rd_2), .Rs_Id_nEx(Rs_1), .Rs_If___ID(Imm_8), .Branch(Branch), .Rd_If_ID(Rd),
    .Rt_Id_nEx(Rt_1), .Rt0(Rt0), .WB_Output(\output ), .Rd_ID___Ex(Rd_1), .reg___Write_1(re_write_1),
    .Rd_Mem_Wb(Rd_3), .reg___Write_2(re_write_2), .reg___Write_3(re_write_3), .Op_Code_1(opcode_1),
    .Mem_Read(Mem_Read_1), .Pc_Next(main_control[16:13]), .Pc_In(Pc_In_t), .Pc_Out(Pc_Out),
    .Forward_B(Forward_B), .Forward_A(Forward_A), .Forward_E(Forward_E), .Rt_in(Rt_in), .Rs_in(Rs__in),
    .Forward_H(Forward_H), .Forward_G(Forward_G), .Hazard_Out(Hazard_Out), .PC_Hold(Hold_PC),
    .Flush_Id(Flush_ID), .Flush_IF(Flush_IF), .Flush_Sele(Flush_Select), .No_op(No_Op),
    .Forward_D(Forward_D), .Forward_C(Forward_C));
  // Probe on ALu_Output
  // Probe on Rd_data_2
  RAM #(.addrWidth(18), .dataWidth(32), .bus("separate")) ram_2 (
    .addr(ALu_Output[17:0]), .din(Rd_data_2), .data(Data_Mem_Output), .str(Mem_Write_2), .sel(1'b1),
    .clk(clock), .ld(Mem_Read_2), .clr(in_3));
  // Probe on Data_Mem_Output
  MEM_WB mem_wb_1 (
    .ALU_out_MEM(ALu_Output), .Memory_Data_MEM(Data_Mem_Output), .RD_MEM(Rd_2),
    .ALU_Out_WB(mem_wb_1_alu_out_wb), .Memory_Data_WB(mem_wb_1_memory_data_wb), .RD_WB(Rd_3), .CLK(clock),
    .re_write_2(re_write_2), .re_write_3(re_write_3), .Mem_to_Reg_2(Mem_to_reg_2),
    .Mem_to_Reg_3(Mem_to_reg_3), .Rd_Mem_2(Rd_data_2), .RD_WB_2(Rd_data_3), .PC_2(Pc_2_2), .PC_2_2(Pc_2_3));
  // Probe on \output 
  Multiplexer #(.select(2), .width(32)) multiplexer_16 (
    .in0(mem_wb_1_alu_out_wb), .in1(mem_wb_1_memory_data_wb), .in2(Pc_2_3), .out(\output ), .sel(Mem_to_reg_3));  // open: in3, en

  // Other names for the same wires on the sheet: Imm_5[1:0] = \function ; Imm_8[4:0] = {Imm_5, \function };
  //   Imm_11[7:0] = {Imm_8, Imm_5, \function }; RT[2:0] = Imm_5; RS[2:0] = Imm_8;
  //   main_control (some bits) = {Imm_Selct, Imm_In, c_in, Branch, alu_src, en, alu_op};
  //   red___dest[1:0] = main_control[6:5]; re_write = main_control[7]; Mem_Write = main_control[9];
  //   Mem_Read = main_control[10]; Mem_to_reg[1:0] = main_control[12:11]; Pc_Next[3:0] = main_control[16:13];
  //   shift_selector[1:0] = main_control[20:19]; Rt____RD = main_control[21]; Set___Sset = main_control[23];
  //   pc0[19:0] = if_detect

  // Notes on the sheet:
  //   Data Mem
endmodule

module Reg_File (
  input  [2:0] Rd,
  input  [2:0] Ra,
  input  [2:0] Rb,
  input  [31:0] Bus_W,
  input  clock,
  input  in_6,
  input  read_write,
  output [31:0] Rs,
  output [31:0] Rt,
  output [31:0] RD_2
);

  wire and_1_out, and_2_out, and_3_out, and_4_out, and_5_out, and_6_out, and_7_out, and_8_out,
       decoder_1_out0, decoder_1_out1, decoder_1_out2, decoder_1_out3, decoder_1_out4, decoder_1_out5,
       decoder_1_out6, decoder_1_out7, decoder_2_out0, decoder_2_out1, decoder_2_out2, decoder_2_out3,
       decoder_2_out4, decoder_2_out5, decoder_2_out6, decoder_2_out7, decoder_3_out0, decoder_3_out1,
       decoder_3_out2, decoder_3_out3, decoder_3_out4, decoder_3_out5, decoder_3_out6, decoder_3_out7;
  wire [31:0] register_1_q, register_2_q, register_3_q, register_4_q, register_5_q, register_6_q,
       register_7_q, register_8_q;

  Decoder #(.select(3)) decoder_1 (
    .out0(decoder_1_out0), .out1(decoder_1_out1), .out2(decoder_1_out2), .out3(decoder_1_out3),
    .out4(decoder_1_out4), .out5(decoder_1_out5), .out6(decoder_1_out6), .out7(decoder_1_out7), .sel(Rd));  // open: en
  // Probe on Bus_W
  and and_1 (and_1_out, decoder_1_out0, read_write);
  and and_2 (and_2_out, decoder_1_out1, read_write);
  and and_3 (and_3_out, decoder_1_out2, read_write);
  and and_4 (and_4_out, decoder_1_out3, read_write);
  and and_5 (and_5_out, decoder_1_out4, read_write);
  and and_6 (and_6_out, decoder_1_out5, read_write);
  and and_7 (and_7_out, decoder_1_out6, read_write);
  and and_8 (and_8_out, decoder_1_out7, read_write);
  Register #(.width(32)) register_1 (.D(Bus_W), .en(and_1_out), .Q(register_1_q), .clk(clock), .clr(in_6));
  Register #(.width(32)) register_2 (.D(Bus_W), .en(and_2_out), .Q(register_2_q), .clk(clock), .clr(in_6));
  Register #(.width(32)) register_3 (.D(Bus_W), .en(and_3_out), .Q(register_3_q), .clk(clock), .clr(in_6));
  Register #(.width(32)) register_4 (.D(Bus_W), .en(and_4_out), .Q(register_4_q), .clk(clock), .clr(in_6));
  Register #(.width(32)) register_5 (.D(Bus_W), .en(and_5_out), .Q(register_5_q), .clk(clock), .clr(in_6));
  Register #(.width(32)) register_6 (.D(Bus_W), .en(and_6_out), .Q(register_6_q), .clk(clock), .clr(in_6));
  Register #(.width(32)) register_7 (.D(Bus_W), .en(and_7_out), .Q(register_7_q), .clk(clock), .clr(in_6));
  Register #(.width(32)) register_8 (.D(Bus_W), .en(and_8_out), .Q(register_8_q), .clk(clock), .clr(in_6));
  assign RD_2 = decoder_1_out0 ? register_1_q : 32'bz;  // Controlled_Buffer controlled_buffer_1
  assign RD_2 = decoder_1_out1 ? register_2_q : 32'bz;  // Controlled_Buffer controlled_buffer_2
  assign RD_2 = decoder_1_out2 ? register_3_q : 32'bz;  // Controlled_Buffer controlled_buffer_3
  assign RD_2 = decoder_1_out3 ? register_4_q : 32'bz;  // Controlled_Buffer controlled_buffer_4
  assign RD_2 = decoder_1_out4 ? register_5_q : 32'bz;  // Controlled_Buffer controlled_buffer_5
  assign RD_2 = decoder_1_out5 ? register_6_q : 32'bz;  // Controlled_Buffer controlled_buffer_6
  assign RD_2 = decoder_1_out6 ? register_7_q : 32'bz;  // Controlled_Buffer controlled_buffer_7
  assign RD_2 = decoder_1_out7 ? register_8_q : 32'bz;  // Controlled_Buffer controlled_buffer_8
  Decoder #(.select(3)) decoder_2 (
    .out0(decoder_2_out0), .out1(decoder_2_out1), .out2(decoder_2_out2), .out3(decoder_2_out3),
    .out4(decoder_2_out4), .out5(decoder_2_out5), .out6(decoder_2_out6), .out7(decoder_2_out7), .sel(Ra));  // open: en
  assign Rs = decoder_2_out0 ? register_1_q : 32'bz;  // Controlled_Buffer controlled_buffer_9
  assign Rs = decoder_2_out1 ? register_2_q : 32'bz;  // Controlled_Buffer controlled_buffer_10
  assign Rs = decoder_2_out2 ? register_3_q : 32'bz;  // Controlled_Buffer controlled_buffer_11
  assign Rs = decoder_2_out3 ? register_4_q : 32'bz;  // Controlled_Buffer controlled_buffer_12
  assign Rs = decoder_2_out4 ? register_5_q : 32'bz;  // Controlled_Buffer controlled_buffer_13
  assign Rs = decoder_2_out5 ? register_6_q : 32'bz;  // Controlled_Buffer controlled_buffer_14
  assign Rs = decoder_2_out6 ? register_7_q : 32'bz;  // Controlled_Buffer controlled_buffer_15
  assign Rs = decoder_2_out7 ? register_8_q : 32'bz;  // Controlled_Buffer controlled_buffer_16
  Decoder #(.select(3)) decoder_3 (
    .out0(decoder_3_out0), .out1(decoder_3_out1), .out2(decoder_3_out2), .out3(decoder_3_out3),
    .out4(decoder_3_out4), .out5(decoder_3_out5), .out6(decoder_3_out6), .out7(decoder_3_out7), .sel(Rb));  // open: en
  assign Rt = decoder_3_out0 ? register_1_q : 32'bz;  // Controlled_Buffer controlled_buffer_17
  assign Rt = decoder_3_out1 ? register_2_q : 32'bz;  // Controlled_Buffer controlled_buffer_18
  assign Rt = decoder_3_out2 ? register_3_q : 32'bz;  // Controlled_Buffer controlled_buffer_19
  assign Rt = decoder_3_out3 ? register_4_q : 32'bz;  // Controlled_Buffer controlled_buffer_20
  assign Rt = decoder_3_out4 ? register_5_q : 32'bz;  // Controlled_Buffer controlled_buffer_21
  assign Rt = decoder_3_out5 ? register_6_q : 32'bz;  // Controlled_Buffer controlled_buffer_22
  assign Rt = decoder_3_out6 ? register_7_q : 32'bz;  // Controlled_Buffer controlled_buffer_23
  assign Rt = decoder_3_out7 ? register_8_q : 32'bz;  // Controlled_Buffer controlled_buffer_24
endmodule

module ALU (
  input  [31:0] RS,
  input  [3:0] ALU_Selector,
  input  [31:0] RT_DATA,
  input  [4:0] Imm_5,
  input  [1:0] shift_selector,
  input  cin,
  input  [7:0] Imm_8,
  output [31:0] alu_out,
  output out_9
);

  wire comparator_1_eq, comparator_1_lt, not_1_out;
  wire [31:0] adder_and_sub_1_result, and_1_out, bit_extender_1_out, bit_extender_2_out, bit_extender_3_out,
       bit_extender_4_out, multiplexer_1_out, or_1_out, shifter_1_out, shifter_2_out, shifter_3_out,
       shifter_4_out, xnor_1_out, xor_1_out;

  adder_and_sub adder_and_sub_1 (
    .RS_DATA(RS), .in_2(cin), .RT_DATA(RT_DATA), .result(adder_and_sub_1_result), .overflow(out_9));  // open: C31, C1
  Comparator_part #(.width(32)) comparator_1 (
    .a(RS), .b(RT_DATA), .eq(comparator_1_eq), .lt(comparator_1_lt));  // open: gt
  assign and_1_out = RS & RT_DATA;  // AND_Gate and_1, 32 bits wide
  assign or_1_out = RS | RT_DATA;  // OR_Gate or_1, 32 bits wide
  assign xor_1_out = RS ^ RT_DATA;  // XOR_Gate xor_1, 32 bits wide
  assign xnor_1_out = ~(RS ^ RT_DATA);  // XNOR_Gate xnor_1, 32 bits wide
  Shifter #(.width(32)) shifter_1 (.in(RS), .\dist (Imm_5), .out(shifter_1_out));
  Shifter #(.width(32), .shift("lr")) shifter_2 (.in(RS), .\dist (Imm_5), .out(shifter_2_out));
  Shifter #(.width(32), .shift("ar")) shifter_3 (.in(RS), .\dist (Imm_5), .out(shifter_3_out));
  Shifter #(.width(32), .shift("rr")) shifter_4 (.in(RS), .\dist (Imm_5), .out(shifter_4_out));
  assign bit_extender_1_out = {{31{1'b0}}, not_1_out};  // Bit_Extender bit_extender_1
  not not_1 (not_1_out, comparator_1_eq);
  assign bit_extender_2_out = {{31{1'b0}}, comparator_1_lt};  // Bit_Extender bit_extender_2
  assign bit_extender_3_out = {{24{Imm_8[7]}}, Imm_8};  // Bit_Extender bit_extender_3
  Multiplexer #(.select(2), .width(32)) multiplexer_1 (
    .in0(shifter_1_out), .in1(shifter_2_out), .in2(shifter_3_out), .in3(shifter_4_out),
    .out(multiplexer_1_out), .sel(shift_selector));  // open: en
  assign bit_extender_4_out = {{31{1'b0}}, comparator_1_eq};  // Bit_Extender bit_extender_4
  Multiplexer #(.select(4), .width(32)) multiplexer_2 (
    .in0(and_1_out), .in1(or_1_out), .in2(xor_1_out), .in3(adder_and_sub_1_result), .in4(xnor_1_out),
    .in5(multiplexer_1_out), .in7(bit_extender_2_out), .in8(bit_extender_4_out), .in9(bit_extender_1_out),
    .in10(bit_extender_4_out), .in11({RT_DATA[23:0], Imm_8}), .in12(bit_extender_3_out), .out(alu_out),
    .sel(ALU_Selector));  // open: in6, in13, in14, in15, en
endmodule

module adder_and_sub (
  input  [31:0] RS_DATA,
  input  in_2,
  input  [31:0] RT_DATA,
  output [31:0] result,
  output C31,
  output C1,
  output overflow
);

  wire inputB1;
  wire [30:0] inputB31;
  wire [31:0] bit_extender_1_out;

  assign bit_extender_1_out = {{31{in_2}}, in_2};  // Bit_Extender bit_extender_1
  assign inputB31 = bit_extender_1_out[30:0] ^ RT_DATA[30:0];  // XOR_Gate xor_1, 31 bits wide
  xor xor_2 (inputB1, bit_extender_1_out[31], RT_DATA[31]);
  Adder #(.width(31)) adder_1 (.a(RS_DATA[30:0]), .b(inputB31), .out(result[30:0]), .cin(in_2), .cout(C31));
  Adder #(.width(1)) adder_2 (.a(RS_DATA[31]), .b(inputB1), .out(result[31]), .cin(C31), .cout(C1));
  xor xor_3 (overflow, C31, C1);

  // Other names for the same wires on the sheet: inputA31[30:0] = RS_DATA[30:0]; inputA1 = RS_DATA[31]
endmodule

module Control_Unit (
  input  [1:0] \function ,
  input  [4:0] Op_Code,
  output [3:0] alu_op,
  output en,
  output [1:0] regdest,
  output re_wr,
  output alu_src,
  output mem_write,
  output mem_read,
  output [1:0] mem_to_reg,
  output [3:0] pc_next,
  output branch,
  output c_in,
  output [1:0] shift_select,
  output rt__rd,
  output imm_in,
  output set__sset,
  output [1:0] imm_selector
);

  wire [25:0] add, addi, \and , andi, beq, BEQZ, BGEZ, BGTZ, BLEZ, BLTZ, BNEZ, bnq, eqv, eqvi, J, JAL, JALR,
       JR, lw, multiplexer_1_out, multiplexer_2_out, \or , ori, ror, seq, seqi, SET, sll, slt, slti, srl,
       SSET, sub, sw, Xor, xori;

  \and  and_1 (
    .alu_op(\and [3:0]), .en(\and [4]), .regdest(\and [6:5]), .re_wr(\and [7]), .alu_src(\and [8]),
    .mem_write(\and [9]), .mem_read(\and [10]), .mem_to_reg(\and [12:11]), .pc_next(\and [16:13]),
    .branch(\and [17]), .c_in(\and [18]), .shift_select(\and [20:19]), .rt___rd(\and [21]),
    .imm_in(\and [22]), .set___sset(\and [23]), .imm_selctor(\and [25:24]));
  \or  or_1 (
    .alu_op(\or [3:0]), .en(\or [4]), .regdest(\or [6:5]), .re_wr(\or [7]), .alu_src(\or [8]),
    .mem_write(\or [9]), .mem_read(\or [10]), .mem_to_reg(\or [12:11]), .pc_next(\or [16:13]),
    .branch(\or [17]), .c_in(\or [18]), .shift_select(\or [20:19]), .rt___rd(\or [21]), .imm_in(\or [22]),
    .set___sset(\or [23]), .imm_selctor(\or [25:24]));
  \xor  xor_1 (
    .alu_op(Xor[3:0]), .en(Xor[4]), .regdest(Xor[6:5]), .re_wr(Xor[7]), .alu_src(Xor[8]), .mem_write(Xor[9]),
    .mem_read(Xor[10]), .mem_to_reg(Xor[12:11]), .pc_next(Xor[16:13]), .branch(Xor[17]), .c_in(Xor[18]),
    .shift_select(Xor[20:19]), .rt___rd(Xor[21]), .imm_in(Xor[22]), .set___sset(Xor[23]),
    .imm_selctor(Xor[25:24]));
  eqv eqv_1 (
    .alu_op(eqv[3:0]), .en(eqv[4]), .regdest(eqv[6:5]), .re_wr(eqv[7]), .alu_src(eqv[8]), .mem_write(eqv[9]),
    .mem_read(eqv[10]), .mem_to_reg(eqv[12:11]), .pc_next(eqv[16:13]), .branch(eqv[17]), .c_in(eqv[18]),
    .shift_select(eqv[20:19]), .rt___rd(eqv[21]), .imm_in(eqv[22]), .set___sset(eqv[23]),
    .imm_selctor(eqv[25:24]));
  add add_1 (
    .alu_op(add[3:0]), .en(add[4]), .regdest(add[6:5]), .re_wr(add[7]), .alu_src(add[8]), .mem_write(add[9]),
    .mem_read(add[10]), .mem_to_reg(add[12:11]), .pc_next(add[16:13]), .branch(add[17]), .c_in(add[18]),
    .shift_select(add[20:19]), .rt___rd(add[21]), .imm_in(add[22]), .set___sset(add[23]),
    .imm_selctor(add[25:24]));
  sub sub_1 (
    .alu_op(sub[3:0]), .en(sub[4]), .regdest(sub[6:5]), .re_wr(sub[7]), .alu_src(sub[8]), .mem_write(sub[9]),
    .mem_read(sub[10]), .mem_to_reg(sub[12:11]), .pc_next(sub[16:13]), .branch(sub[17]), .c_in(sub[18]),
    .shift_select(sub[20:19]), .rt___rd(sub[21]), .imm_in(sub[22]), .set___sset(sub[23]),
    .imm_selctor(sub[25:24]));
  seq seq_1 (
    .alu_op(seq[3:0]), .en(seq[4]), .regdest(seq[6:5]), .re_wr(seq[7]), .alu_src(seq[8]), .mem_write(seq[9]),
    .mem_read(seq[10]), .mem_to_reg(seq[12:11]), .pc_next(seq[16:13]), .branch(seq[17]), .c_in(seq[18]),
    .shift_select(seq[20:19]), .rt___rd(seq[21]), .imm_in(seq[22]), .set___sset(seq[23]),
    .imm_selctor(seq[25:24]));
  slt slt_1 (
    .alu_op(slt[3:0]), .en(slt[4]), .regdest(slt[6:5]), .re_wr(slt[7]), .alu_src(slt[8]), .mem_write(slt[9]),
    .mem_read(slt[10]), .mem_to_reg(slt[12:11]), .pc_next(slt[16:13]), .branch(slt[17]), .c_in(slt[18]),
    .shift_select(slt[20:19]), .rt___rd(slt[21]), .imm_in(slt[22]), .set___sset(slt[23]),
    .imm_selctor(slt[25:24]));
  andi andi_1 (
    .alu_op(andi[3:0]), .en(andi[4]), .regdest(andi[6:5]), .re_wr(andi[7]), .alu_src(andi[8]),
    .mem_write(andi[9]), .mem_read(andi[10]), .mem_to_reg(andi[12:11]), .pc_next(andi[16:13]),
    .branch(andi[17]), .c_in(andi[18]), .shift_select(andi[20:19]), .rt___rd(andi[21]), .imm_in(andi[22]),
    .set___sset(andi[23]), .imm_selctor(andi[25:24]));
  xori xori_1 (
    .alu_op(xori[3:0]), .en(xori[4]), .regdest(xori[6:5]), .re_wr(xori[7]), .alu_src(xori[8]),
    .mem_write(xori[9]), .mem_read(xori[10]), .mem_to_reg(xori[12:11]), .pc_next(xori[16:13]),
    .branch(xori[17]), .c_in(xori[18]), .shift_select(xori[20:19]), .rt___rd(xori[21]), .imm_in(xori[22]),
    .set___sset(xori[23]), .imm_selctor(xori[25:24]));
  eqvi eqvi_1 (
    .alu_op(eqvi[3:0]), .en(eqvi[4]), .regdest(eqvi[6:5]), .re_wr(eqvi[7]), .alu_src(eqvi[8]),
    .mem_write(eqvi[9]), .mem_read(eqvi[10]), .mem_to_reg(eqvi[12:11]), .pc_next(eqvi[16:13]),
    .branch(eqvi[17]), .c_in(eqvi[18]), .shift_select(eqvi[20:19]), .rt___rd(eqvi[21]), .imm_in(eqvi[22]),
    .set___sset(eqvi[23]), .imm_selctor(eqvi[25:24]));
  addi addi_1 (
    .alu_op(addi[3:0]), .en(addi[4]), .regdest(addi[6:5]), .re_wr(addi[7]), .alu_src(addi[8]),
    .mem_write(addi[9]), .mem_read(addi[10]), .mem_to_reg(addi[12:11]), .pc_next(addi[16:13]),
    .branch(addi[17]), .c_in(addi[18]), .shift_select(addi[20:19]), .rt___rd(addi[21]), .imm_in(addi[22]),
    .set___sset(addi[23]), .imm_selctor(addi[25:24]));
  slti slti_1 (
    .alu_op(slti[3:0]), .en(slti[4]), .regdest(slti[6:5]), .re_wr(slti[7]), .alu_src(slti[8]),
    .mem_write(slti[9]), .mem_read(slti[10]), .mem_to_reg(slti[12:11]), .pc_next(slti[16:13]),
    .branch(slti[17]), .c_in(slti[18]), .shift_select(slti[20:19]), .rt___rd(slti[21]), .imm_in(slti[22]),
    .set___sset(slti[23]), .imm_selctor(slti[25:24]));
  beq beq_1 (
    .alu_op(beq[3:0]), .en(beq[4]), .regdest(beq[6:5]), .re_wr(beq[7]), .alu_src(beq[8]), .mem_write(beq[9]),
    .mem_read(beq[10]), .mem_to_reg(beq[12:11]), .pc_next(beq[16:13]), .branch(beq[17]), .c_in(beq[18]),
    .shift_select(beq[20:19]), .rt___rd(beq[21]), .imm_in(beq[22]), .set___sset(beq[23]),
    .imm_selctor(beq[25:24]));
  bnq bnq_1 (
    .alu_op(bnq[3:0]), .en(bnq[4]), .regdest(bnq[6:5]), .re_wr(bnq[7]), .alu_src(bnq[8]), .mem_write(bnq[9]),
    .mem_read(bnq[10]), .mem_to_reg(bnq[12:11]), .pc_next(bnq[16:13]), .branch(bnq[17]), .c_in(bnq[18]),
    .shift_select(bnq[20:19]), .rt___rd(bnq[21]), .imm_in(bnq[22]), .set___sset(bnq[23]),
    .imm_selctor(bnq[25:24]));
  ori ori_1 (
    .alu_op(ori[3:0]), .en(ori[4]), .regdest(ori[6:5]), .re_wr(ori[7]), .alu_src(ori[8]), .mem_write(ori[9]),
    .mem_read(ori[10]), .mem_to_reg(ori[12:11]), .pc_next(ori[16:13]), .branch(ori[17]), .c_in(ori[18]),
    .shift_select(ori[20:19]), .rt___rd(ori[21]), .imm_in(ori[22]), .set___sset(ori[23]),
    .imm_selctor(ori[25:24]));
  seqi seqi_1 (
    .alu_op(seqi[3:0]), .en(seqi[4]), .regdest(seqi[6:5]), .re_wr(seqi[7]), .alu_src(seqi[8]),
    .mem_write(seqi[9]), .mem_read(seqi[10]), .mem_to_reg(seqi[12:11]), .pc_next(seqi[16:13]),
    .branch(seqi[17]), .c_in(seqi[18]), .shift_select(seqi[20:19]), .rt___rd(seqi[21]), .imm_in(seqi[22]),
    .set___sset(seqi[23]), .imm_selctor(seqi[25:24]));
  sll sll_1 (
    .alu_op(sll[3:0]), .en(sll[4]), .regdest(sll[6:5]), .re_wr(sll[7]), .alu_src(sll[8]), .mem_write(sll[9]),
    .mem_read(sll[10]), .mem_to_reg(sll[12:11]), .pc_next(sll[16:13]), .branch(sll[17]), .c_in(sll[18]),
    .shift_select(sll[20:19]), .rt___rd(sll[21]), .imm_in(sll[22]), .set___sset(sll[23]),
    .imm_selctor(sll[25:24]));
  srl srl_1 (
    .alu_op(srl[3:0]), .en(srl[4]), .regdest(srl[6:5]), .re_wr(srl[7]), .alu_src(srl[8]), .mem_write(srl[9]),
    .mem_read(srl[10]), .mem_to_reg(srl[12:11]), .pc_next(srl[16:13]), .branch(srl[17]), .c_in(srl[18]),
    .shift_select(srl[20:19]), .rt___rd(srl[21]), .imm_in(srl[22]), .set___sset(srl[23]),
    .imm_selctor(srl[25:24]));
  ror ror_1 (
    .alu_op(ror[3:0]), .en(ror[4]), .regdest(ror[6:5]), .re_wr(ror[7]), .alu_src(ror[8]), .mem_write(ror[9]),
    .mem_read(ror[10]), .mem_to_reg(ror[12:11]), .pc_next(ror[16:13]), .branch(ror[17]), .c_in(ror[18]),
    .shift_select(ror[20:19]), .rt___rd(ror[21]), .imm_in(ror[22]), .set___sset(ror[23]),
    .imm_selctor(ror[25:24]));
  set set_1 (
    .alu_op(SET[3:0]), .en(SET[4]), .regdest(SET[6:5]), .re_wr(SET[7]), .alu_src(SET[8]), .mem_write(SET[9]),
    .mem_read(SET[10]), .mem_to_reg(SET[12:11]), .pc_next(SET[16:13]), .branch(SET[17]), .c_in(SET[18]),
    .shift_select(SET[20:19]), .rt___rd(SET[21]), .imm_in(SET[22]), .set___sset(SET[23]),
    .imm_selctor(SET[25:24]));
  SSet sset_1 (
    .alu_op(SSET[3:0]), .en(SSET[4]), .regdest(SSET[6:5]), .re_wr(SSET[7]), .alu_src(SSET[8]),
    .mem_write(SSET[9]), .mem_read(SSET[10]), .mem_to_reg(SSET[12:11]), .pc_next(SSET[16:13]),
    .branch(SSET[17]), .c_in(SSET[18]), .shift_select(SSET[20:19]), .rt___rd(SSET[21]), .imm_in(SSET[22]),
    .set___sset(SSET[23]), .imm_selctor(SSET[25:24]));
  Beqz beqz_1 (
    .alu_op(BEQZ[3:0]), .en(BEQZ[4]), .regdest(BEQZ[6:5]), .re_wr(BEQZ[7]), .alu_src(BEQZ[8]),
    .mem_write(BEQZ[9]), .mem_read(BEQZ[10]), .mem_to_reg(BEQZ[12:11]), .pc_next(BEQZ[16:13]),
    .branch(BEQZ[17]), .c_in(BEQZ[18]), .shift_select(BEQZ[20:19]), .rt___rd(BEQZ[21]), .imm_in(BEQZ[22]),
    .set___sset(BEQZ[23]), .imm_selctor(BEQZ[25:24]));
  Bnez bnez_1 (
    .alu_op(BNEZ[3:0]), .en(BNEZ[4]), .regdest(BNEZ[6:5]), .re_wr(BNEZ[7]), .alu_src(BNEZ[8]),
    .mem_write(BNEZ[9]), .mem_read(BNEZ[10]), .mem_to_reg(BNEZ[12:11]), .out_9(BNEZ[16:13]),
    .branch(BNEZ[17]), .c_in(BNEZ[18]), .shift_select(BNEZ[20:19]), .rt___rd(BNEZ[21]), .imm_in(BNEZ[22]),
    .set___sset(BNEZ[23]), .imm_selctor(BNEZ[25:24]));
  Bltz bltz_1 (
    .alu_op(BLTZ[3:0]), .en(BLTZ[4]), .regdest(BLTZ[6:5]), .re_wr(BLTZ[7]), .alu_src(BLTZ[8]),
    .mem_write(BLTZ[9]), .mem_read(BLTZ[10]), .mem_to_reg(BLTZ[12:11]), .pc_next(BLTZ[16:13]),
    .branch(BLTZ[17]), .c_in(BLTZ[18]), .shift_select(BLTZ[20:19]), .rt___rd(BLTZ[21]), .imm_in(BLTZ[22]),
    .set___sset(BLTZ[23]), .imm_selctor(BLTZ[25:24]));
  Bgez bgez_1 (
    .alu_op(BGEZ[3:0]), .en(BGEZ[4]), .regdest(BGEZ[6:5]), .re_wr(BGEZ[7]), .alu_src(BGEZ[8]),
    .mem_write(BGEZ[9]), .mem_read(BGEZ[10]), .mem_to_reg(BGEZ[12:11]), .pc_next(BGEZ[16:13]),
    .branch(BGEZ[17]), .c_in(BGEZ[18]), .shift_select(BGEZ[20:19]), .rt___rd(BGEZ[21]), .imm_in(BGEZ[22]),
    .set___sset(BGEZ[23]), .imm_selctor(BGEZ[25:24]));
  JR jr_1 (
    .alu_op(JR[3:0]), .en(JR[4]), .regdest(JR[6:5]), .re_wr(JR[7]), .alu_src(JR[8]), .mem_write(JR[9]),
    .mem_read(JR[10]), .mem_to_reg(JR[12:11]), .pc_next(JR[16:13]), .branch(JR[17]), .c_in(JR[18]),
    .shift_select(JR[20:19]), .rt___rd(JR[21]), .imm_in(JR[22]), .set___sset(JR[23]), .imm_selctor(JR[25:24]));
  lw lw_1 (
    .alu_op(lw[3:0]), .en(lw[4]), .regdest(lw[6:5]), .re_wr(lw[7]), .alu_src(lw[8]), .mem_write(lw[9]),
    .mem_read(lw[10]), .mem_to_reg(lw[12:11]), .pc_next(lw[16:13]), .branch(lw[17]), .c_in(lw[18]),
    .shift_select(lw[20:19]), .rt___rd(lw[21]), .imm_in(lw[22]), .set___sset(lw[23]), .imm_selctor(lw[25:24]));
  sw sw_1 (
    .alu_op(sw[3:0]), .en(sw[4]), .regdest(sw[6:5]), .re_wr(sw[7]), .alu_src(sw[8]), .mem_write(sw[9]),
    .mem_read(sw[10]), .mem_to_reg(sw[12:11]), .pc_next(sw[16:13]), .branch(sw[17]), .c_in(sw[18]),
    .shift_select(sw[20:19]), .rt___rd(sw[21]), .imm_in(sw[22]), .set___sset(sw[23]), .imm_selctor(sw[25:24]));
  Jalr jalr_1 (
    .alu_op(JALR[3:0]), .en(JALR[4]), .regdest(JALR[6:5]), .re_wr(JALR[7]), .alu_src(JALR[8]),
    .mem_write(JALR[9]), .mem_read(JALR[10]), .mem_to_reg(JALR[12:11]), .pc_next(JALR[16:13]),
    .branch(JALR[17]), .c_in(JALR[18]), .shift_select(JALR[20:19]), .rt___rd(JALR[21]), .imm_in(JALR[22]),
    .set___sset(JALR[23]), .imm_selctor(JALR[25:24]));
  Jal jal_1 (
    .alu_op(JAL[3:0]), .en(JAL[4]), .regdest(JAL[6:5]), .re_wr(JAL[7]), .alu_src(JAL[8]), .mem_write(JAL[9]),
    .mem_read(JAL[10]), .mem_to_reg(JAL[12:11]), .pc_next(JAL[16:13]), .branch(JAL[17]), .c_in(JAL[18]),
    .shift_select(JAL[20:19]), .rt___rd(JAL[21]), .imm_in(JAL[22]), .set___sset(JAL[23]),
    .imm_selctor(JAL[25:24]));
  J j_1 (
    .alu_op(J[3:0]), .en(J[4]), .regdest(J[6:5]), .re_wr(J[7]), .alu_src(J[8]), .mem_write(J[9]),
    .mem_read(J[10]), .mem_to_reg(J[12:11]), .pc_next(J[16:13]), .branch(J[17]), .c_in(J[18]),
    .shift_select(J[20:19]), .rt___rd(J[21]), .imm_in(J[22]), .set___sset(J[23]), .imm_selctor(J[25:24]));
  Blez blez_1 (
    .alu_op(BLEZ[3:0]), .en(BLEZ[4]), .regdest(BLEZ[6:5]), .re_wr(BLEZ[7]), .alu_src(BLEZ[8]),
    .mem_write(BLEZ[9]), .mem_read(BLEZ[10]), .mem_to_reg(BLEZ[12:11]), .pc_next(BLEZ[16:13]),
    .branch(BLEZ[17]), .c_in(BLEZ[18]), .shift_select(BLEZ[20:19]), .rt___rd(BLEZ[21]), .imm_in(BLEZ[22]),
    .set___sset(BLEZ[23]), .imm_selctor(BLEZ[25:24]));
  Bjtz bjtz_1 (
    .alu_op(BGTZ[3:0]), .en(BGTZ[4]), .regdest(BGTZ[6:5]), .re_wr(BGTZ[7]), .alu_src(BGTZ[8]),
    .mem_write(BGTZ[9]), .mem_read(BGTZ[10]), .mem_to_reg(BGTZ[12:11]), .pc_next(BGTZ[16:13]),
    .branch(BGTZ[17]), .c_in(BGTZ[18]), .shift_select(BGTZ[20:19]), .rt___rd(BGTZ[21]), .imm_in(BGTZ[22]),
    .set___sset(BGTZ[23]), .imm_selctor(BGTZ[25:24]));
  Multiplexer #(.select(2), .width(26)) multiplexer_1 (
    .in0(\and ), .in1(\or ), .in2(Xor), .in3(eqv), .out(multiplexer_1_out), .sel(\function ));  // open: en
  Multiplexer #(.select(2), .width(26)) multiplexer_2 (
    .in0(add), .in1(sub), .in2(slt), .in3(seq), .out(multiplexer_2_out), .sel(\function ));  // open: en
  Multiplexer #(.select(5), .width(26)) multiplexer_3 (
    .in0(multiplexer_1_out), .in1(multiplexer_2_out), .in2({26{1'b0}}), .in3({26{1'b0}}), .in4(andi),
    .in5(ori), .in6(xori), .in7(eqvi), .in8(addi), .in9(slti), .in10(seqi), .in11(sll), .in12(srl),
    .in13(ror), .in14(beq), .in15(bnq), .in16(lw), .in17(sw), .in18({26{1'b0}}), .in19({26{1'b0}}),
    .in20(BEQZ), .in21(BNEZ), .in22(BLTZ), .in23(BGEZ), .in24(BGTZ), .in25(BLEZ), .in26(JR), .in27(JALR),
    .in28(SET), .in29(SSET), .in30(J), .in31(JAL),
    .out({imm_selector, set__sset, imm_in, rt__rd, shift_select, c_in, branch, pc_next, mem_to_reg, mem_read, mem_write, alu_src, re_wr, regdest, en, alu_op}),
    .sel(Op_Code));  // open: en
endmodule

module PC (
  input  [19:0] J___JAL,
  input  [19:0] JALR,
  input  [19:0] \input ,
  input  beq,
  input  bnq,
  input  beqz,
  input  [19:0] pc,
  input  bnez,
  input  bltz,
  input  bgeZ,
  input  [3:0] in_11,
  input  [19:0] immediate,
  input  bgtz,
  input  blez,
  input  branch,
  input  [19:0] JR,
  output [19:0] \output 
);

  wire and_1_out, and_2_out, and_3_out, and_4_out, and_5_out, and_6_out, and_7_out, and_8_out;
  wire [19:0] adder_1_out, adder_2_out, adder_3_out, adder_4_out, adder_5_out, adder_6_out, adder_7_out,
       adder_8_out, adder_9_out, multiplexer_1_out, multiplexer_2_out, multiplexer_3_out, multiplexer_4_out,
       multiplexer_5_out, multiplexer_6_out, multiplexer_7_out, multiplexer_8_out;

  Adder #(.width(20)) adder_1 (.a(20'h2), .b(\input ), .out(adder_1_out));  // open: cin, cout
  Adder #(.width(20)) adder_2 (.a(pc), .b(immediate), .out(adder_2_out));  // open: cin, cout
  and and_1 (and_1_out, branch, beq);
  Multiplexer #(.width(20)) multiplexer_1 (
    .in0(adder_1_out), .in1(adder_2_out), .out(multiplexer_1_out), .sel(and_1_out));  // open: en
  Adder #(.width(20)) adder_3 (.a(pc), .b(immediate), .out(adder_3_out));  // open: cin, cout
  and and_2 (and_2_out, branch, bnq);
  Multiplexer #(.width(20)) multiplexer_2 (
    .in0(adder_1_out), .in1(adder_3_out), .out(multiplexer_2_out), .sel(and_2_out));  // open: en
  Adder #(.width(20)) adder_4 (.a(pc), .b(immediate), .out(adder_4_out));  // open: cin, cout
  Multiplexer #(.width(20)) multiplexer_3 (
    .in0(adder_1_out), .in1(adder_4_out), .out(multiplexer_3_out), .sel(and_3_out));  // open: en
  and and_3 (and_3_out, branch, beqz);
  Adder #(.width(20)) adder_5 (.a(pc), .b(immediate), .out(adder_5_out));  // open: cin, cout
  Multiplexer #(.width(20)) multiplexer_4 (
    .in0(adder_1_out), .in1(adder_5_out), .out(multiplexer_4_out), .sel(and_4_out));  // open: en
  and and_4 (and_4_out, branch, bnez);
  Adder #(.width(20)) adder_6 (.a(pc), .b(immediate), .out(adder_6_out));  // open: cin, cout
  Multiplexer #(.width(20)) multiplexer_5 (
    .in0(adder_1_out), .in1(adder_6_out), .out(multiplexer_5_out), .sel(and_5_out));  // open: en
  and and_5 (and_5_out, branch, bltz);
  Adder #(.width(20)) adder_7 (.a(pc), .b(immediate), .out(adder_7_out));  // open: cin, cout
  Multiplexer #(.width(20)) multiplexer_6 (
    .in0(adder_1_out), .in1(adder_7_out), .out(multiplexer_6_out), .sel(and_6_out));  // open: en
  and and_6 (and_6_out, branch, bgeZ);
  Adder #(.width(20)) adder_8 (.a(pc), .b(immediate), .out(adder_8_out));  // open: cin, cout
  Multiplexer #(.width(20)) multiplexer_7 (
    .in0(adder_1_out), .in1(adder_8_out), .out(multiplexer_7_out), .sel(and_7_out));  // open: en
  and and_7 (and_7_out, branch, bgtz);
  Multiplexer #(.width(20)) multiplexer_8 (
    .in0(adder_1_out), .in1(adder_9_out), .out(multiplexer_8_out), .sel(and_8_out));  // open: en
  Adder #(.width(20)) adder_9 (.a(pc), .b(immediate), .out(adder_9_out));  // open: cin, cout
  and and_8 (and_8_out, branch, blez);
  Multiplexer #(.select(4), .width(20)) multiplexer_9 (
    .in0(multiplexer_1_out), .in1(J___JAL), .in2(JALR), .in3(multiplexer_2_out), .in4(multiplexer_3_out),
    .in5(multiplexer_4_out), .in6(multiplexer_5_out), .in7(multiplexer_6_out), .in8(multiplexer_7_out),
    .in9(multiplexer_8_out), .in10(JR), .in14(adder_1_out), .out(\output ), .sel(in_11));  // open: in11, in12, in13, in15, en
endmodule

module Main_Hazard_Unit (
  input  Clk,
  input  [2:0] Rd_Ex___MEM,
  input  [2:0] Rs_Id_nEx,
  input  [3:0] Pc_Next,
  input  [2:0] Rs_If___ID,
  input  Branch,
  input  [19:0] Pc_Out,
  input  [2:0] Rd_If_ID,
  input  [2:0] Rt_Id_nEx,
  input  [2:0] Rt0,
  input  [31:0] WB_Output,
  input  [2:0] Rd_ID___Ex,
  input  reg___Write_1,
  input  [19:0] Pc_In,
  input  [2:0] Rd_Mem_Wb,
  input  reg___Write_2,
  input  reg___Write_3,
  input  [4:0] Op_Code_1,
  input  Mem_Read,
  output [1:0] Forward_A,
  output [1:0] Forward_B,
  output Rt_in,
  output Rs_in,
  output [1:0] Forward_D,
  output [1:0] Forward_C,
  output PC_Hold,
  output Forward_H,
  output Forward_G,
  output Forward_E,
  output Flush_IF,
  output [31:0] Hazard_Out,
  output No_op,
  output Flush_Sele,
  output Flush_Id
);

  Branch___Jump_Detect branch_jump_detect_1 (
    .PC_Next(Pc_Next), .Branch(Branch), .PC_In(Pc_In), .PC_Out(Pc_Out), .No_Operation(No_op));
  LW_Hazard_Detect lw_hazard_detect_1 (
    .Rd_IF_ID(Rd_If_ID), .IsLW(Mem_Read), .Rd_ID_EX(Rd_ID___Ex), .FlushID(Flush_Id),
    .Flush_Select(Flush_Sele), .StallID(Flush_IF), .in_1(Clk), .StallIF(PC_Hold), .Rs_IF_ID(Rs_If___ID));
  WB_Hazard_Detect wb_hazard_detect_1 (
    .re_write_3(reg___Write_3), .branch(Branch), .WB_RD3(Rd_Mem_Wb), .RT(Rt0), .RS(Rs_If___ID),
    .in_7(WB_Output), .clk_2(Clk), .forward_G(Forward_G), .Foward_H(Forward_H), .out_11(Hazard_Out), .clk(Clk));
  Forward_unit_4 forward_unit_4_1 (
    .clk(Clk), .RS(Rs_If___ID), .RT(Rt0), .RD3(Rd_Mem_Wb), .REG_WRITE_3(reg___Write_3), .ALUCtl(PC_Hold),
    .H(Rs_in), .L(Rt_in));
  Forward_Unit_3 forward_unit_3_1 (
    .RD_MEM_WB(Rd_Mem_Wb), .RD_ID_EX(Rd_ID___Ex), .Forward_E(Forward_E), .Op_Code(Op_Code_1));
  Forward_Unit_2 forward_unit_2_1 (
    .Branch(Branch), .ID_ID_Rs(Rs_If___ID), .EX_MEM_Rd(Rd_Ex___MEM), .IF_ID_RD(Rd_If_ID),
    .ID_EX_Rd(Rd_ID___Ex), .Branch_2(Branch), .Forward_C(Forward_C), .Forward_D(Forward_D));
  Forward_Unit_1 forward_unit_1_1 (
    .REG_WRITE_3(reg___Write_3), .ALUCtl(PC_Hold), .ID_EX_Rs(Rs_Id_nEx), .MEM_WB_Rd(Rd_Mem_Wb),
    .ID_EX_Rt(Rt_Id_nEx), .EX_MEM_Rd(Rd_Ex___MEM), .ID_Ex_Rd(Rd_ID___Ex), .REG_WRITE_2(reg___Write_2),
    .ALUCtl_2(PC_Hold), .Forward_B(Forward_B), .Forward_A(Forward_A), .CLK(Clk));

  // Other names for the same wires on the sheet: Clock = Clk; Hold_PC = PC_Hold; Mem_Read_1 = Mem_Read;
  //   Rs_IF_ID[2:0] = Rs_If___ID; Rt0_IF_ID[2:0] = Rt0
endmodule

module Forward_Unit_1 (
  input  CLK,
  input  REG_WRITE_3,
  input  ALUCtl,
  input  [2:0] ID_EX_Rs,
  input  [2:0] MEM_WB_Rd,
  input  [2:0] ID_EX_Rt,
  input  [2:0] EX_MEM_Rd,
  input  [2:0] ID_Ex_Rd,
  input  REG_WRITE_2,
  input  ALUCtl_2,
  output [1:0] Forward_B,
  output [1:0] Forward_A
);

  wire and_1_out, and_2_out, and_3_out, and_4_out, and_5_out, and_6_out, comparator_1_eq, comparator_2_eq,
       comparator_3_eq, comparator_4_eq, comparator_5_eq, d_ff_1_q, d_ff_2_q, detect_4_clk, detect_clk_3,
       not_1_out, not_2_out, or_1_out;
  wire [1:0] multiplexer_1_out, multiplexer_2_out;

  not not_1 (not_1_out, ALUCtl_2);
  and and_1 (and_1_out, REG_WRITE_3, not_2_out);
  not not_2 (not_2_out, ALUCtl);
  Comparator_part #(.width(3)) comparator_1 (.a(ID_EX_Rs), .b(MEM_WB_Rd), .eq(comparator_1_eq));  // open: gt, lt
  Comparator_part #(.width(3)) comparator_2 (.a(MEM_WB_Rd), .b(ID_EX_Rt), .eq(comparator_2_eq));  // open: gt, lt
  Comparator_part #(.width(3)) comparator_3 (.a(ID_EX_Rt), .b(EX_MEM_Rd), .eq(comparator_3_eq));  // open: gt, lt
  Comparator_part #(.width(3)) comparator_4 (.a(ID_EX_Rs), .b(EX_MEM_Rd), .eq(comparator_4_eq));  // open: gt, lt
  Comparator_part #(.width(3)) comparator_5 (.a(EX_MEM_Rd), .b(ID_Ex_Rd), .eq(comparator_5_eq));  // open: gt, lt
  and and_2 (and_2_out, REG_WRITE_2, not_1_out);
  or or_1 (or_1_out, comparator_3_eq, comparator_5_eq);
  D_Flip_Flop d_ff_1 (.clk(CLK), .D(1'b1), .Q(d_ff_1_q));  // open: Qn, preset, en, reset
  and and_3 (and_3_out, and_1_out, detect_4_clk, comparator_1_eq);
  and and_4 (and_4_out, and_1_out, detect_4_clk, comparator_2_eq);
  and and_5 (and_5_out, comparator_4_eq, detect_clk_3, and_2_out);
  D_Flip_Flop d_ff_2 (.clk(CLK), .D(d_ff_1_q), .Q(d_ff_2_q));  // open: Qn, preset, en, reset
  and and_6 (and_6_out, and_2_out, detect_clk_3, or_1_out);
  D_Flip_Flop d_ff_3 (.clk(CLK), .D(d_ff_2_q), .Q(detect_clk_3));  // open: Qn, preset, en, reset
  D_Flip_Flop d_ff_4 (.clk(CLK), .D(detect_clk_3), .Q(detect_4_clk));  // open: Qn, preset, en, reset
  Multiplexer #(.width(2)) multiplexer_1 (
    .in0(2'b00), .in1(2'b01), .out(multiplexer_1_out), .sel(and_4_out));  // open: en
  Multiplexer #(.width(2)) multiplexer_2 (
    .in0(2'b00), .in1(2'b01), .out(multiplexer_2_out), .sel(and_3_out));  // open: en
  Multiplexer #(.width(2)) multiplexer_3 (
    .in0(multiplexer_1_out), .in1(2'b10), .out(Forward_B), .sel(and_6_out));  // open: en
  Multiplexer #(.width(2)) multiplexer_4 (
    .in0(multiplexer_2_out), .in1(2'b10), .out(Forward_A), .sel(and_5_out));  // open: en
endmodule

module Forward_Unit_2 (
  input  Branch,
  input  [2:0] ID_ID_Rs,
  input  [2:0] EX_MEM_Rd,
  input  [2:0] IF_ID_RD,
  input  [2:0] ID_EX_Rd,
  input  Branch_2,
  output [1:0] Forward_C,
  output [1:0] Forward_D
);

  wire and_1_out, and_2_out, and_3_out, and_4_out, comparator_1_eq, comparator_2_eq, comparator_3_eq,
       comparator_4_eq;
  wire [1:0] multiplexer_1_out, multiplexer_2_out;

  Comparator_part #(.width(3)) comparator_1 (.a(ID_ID_Rs), .b(EX_MEM_Rd), .eq(comparator_1_eq));  // open: gt, lt
  Comparator_part #(.width(3)) comparator_2 (.a(EX_MEM_Rd), .b(IF_ID_RD), .eq(comparator_2_eq));  // open: gt, lt
  Comparator_part #(.width(3)) comparator_3 (.a(IF_ID_RD), .b(ID_EX_Rd), .eq(comparator_3_eq));  // open: gt, lt
  Comparator_part #(.width(3)) comparator_4 (.a(ID_ID_Rs), .b(ID_EX_Rd), .eq(comparator_4_eq));  // open: gt, lt
  and and_1 (and_1_out, Branch, comparator_1_eq);
  and and_2 (and_2_out, Branch, comparator_2_eq);
  and and_3 (and_3_out, comparator_4_eq, Branch_2);
  and and_4 (and_4_out, Branch_2, comparator_3_eq);
  Multiplexer #(.width(2)) multiplexer_1 (
    .in0(2'b00), .in1(2'b01), .out(multiplexer_1_out), .sel(and_2_out));  // open: en
  Multiplexer #(.width(2)) multiplexer_2 (
    .in0(2'b00), .in1(2'b01), .out(multiplexer_2_out), .sel(and_1_out));  // open: en
  Multiplexer #(.width(2)) multiplexer_3 (
    .in0(multiplexer_1_out), .in1(2'b10), .out(Forward_C), .sel(and_4_out));  // open: en
  Multiplexer #(.width(2)) multiplexer_4 (
    .in0(multiplexer_2_out), .in1(2'b10), .out(Forward_D), .sel(and_3_out));  // open: en
endmodule

module Forward_Unit_3 (
  input  [4:0] Op_Code,
  input  [2:0] RD_MEM_WB,
  input  [2:0] RD_ID_EX,
  output Forward_E
);

  wire and_1_out, comparator_1_eq, not_1_out, not_2_out, not_3_out;

  not not_1 (not_1_out, Op_Code[2]);
  not not_2 (not_2_out, Op_Code[3]);
  and and_1 (and_1_out, Op_Code[4], not_2_out, not_1_out, not_3_out, Op_Code[0]);
  not not_3 (not_3_out, Op_Code[1]);
  Comparator_part #(.width(3)) comparator_1 (.a(RD_MEM_WB), .b(RD_ID_EX), .eq(comparator_1_eq));  // open: gt, lt
  and and_2 (Forward_E, and_1_out, comparator_1_eq);
endmodule

// Forward Unit 4
module Forward_unit_4 (
  input  clk,
  input  [2:0] RS,
  input  [2:0] RT,
  input  [2:0] RD3,
  input  REG_WRITE_3,
  input  ALUCtl,
  output H,
  output L
);

  wire and_1_out, comparator_1_eq, comparator_2_eq, d_ff_1_q, d_ff_2_q, d_ff_3_q, d_ff_4_q, not_1_out;

  D_Flip_Flop d_ff_1 (.clk(clk), .D(1'b1), .Q(d_ff_1_q));  // open: Qn, preset, en, reset
  not not_1 (not_1_out, ALUCtl);
  and and_1 (and_1_out, REG_WRITE_3, not_1_out);
  D_Flip_Flop d_ff_2 (.clk(clk), .D(d_ff_1_q), .Q(d_ff_2_q));  // open: Qn, preset, en, reset
  D_Flip_Flop d_ff_3 (.clk(clk), .D(d_ff_2_q), .Q(d_ff_3_q));  // open: Qn, preset, en, reset
  Comparator_part #(.width(3)) comparator_1 (.a(RS), .b(RD3), .eq(comparator_1_eq));  // open: gt, lt
  Comparator_part #(.width(3)) comparator_2 (.a(RT), .b(RD3), .eq(comparator_2_eq));  // open: gt, lt
  D_Flip_Flop d_ff_4 (.clk(clk), .D(d_ff_3_q), .Q(d_ff_4_q));  // open: Qn, preset, en, reset
  and and_2 (H, d_ff_4_q, comparator_1_eq, and_1_out);
  and and_3 (L, d_ff_4_q, comparator_2_eq, and_1_out);
endmodule

module WB_Hazard_Detect (
  input  clk,
  input  re_write_3,
  input  branch,
  input  [2:0] WB_RD3,
  input  [2:0] RT,
  input  [2:0] RS,
  input  [31:0] in_7,
  input  clk_2,
  output forward_G,
  output Foward_H,
  output [31:0] out_11
);

  wire comparator_1_eq, comparator_2_eq, d_ff_1_q, d_ff_2_q, d_ff_3_q, d_ff_4_q;

  Comparator_part #(.width(3)) comparator_1 (.a(WB_RD3), .b(RT), .eq(comparator_1_eq));  // open: gt, lt
  Comparator_part #(.width(3)) comparator_2 (.a(WB_RD3), .b(RS), .eq(comparator_2_eq));  // open: gt, lt
  and and_1 (forward_G, re_write_3, d_ff_4_q, branch, comparator_1_eq);
  D_Flip_Flop d_ff_1 (.clk(clk), .D(1'b1), .Q(d_ff_1_q));  // open: Qn, preset, en, reset
  and and_2 (Foward_H, re_write_3, d_ff_4_q, branch, comparator_2_eq);
  Register #(.width(32), .trigger("high")) register_1 (.D(in_7), .en(1'b1), .Q(out_11), .clk(clk_2), .clr(1'b0));
  D_Flip_Flop d_ff_2 (.clk(clk), .D(d_ff_1_q), .Q(d_ff_2_q));  // open: Qn, preset, en, reset
  D_Flip_Flop d_ff_3 (.clk(clk), .D(d_ff_2_q), .Q(d_ff_3_q));  // open: Qn, preset, en, reset
  D_Flip_Flop d_ff_4 (.clk(clk), .D(d_ff_3_q), .Q(d_ff_4_q));  // open: Qn, preset, en, reset
endmodule

module Branch___Jump_Detect (
  input  [3:0] PC_Next,
  input  Branch,
  input  [19:0] PC_In,
  input  [19:0] PC_Out,
  output No_Operation
);

  wire and_1_out, comparator_1_eq, comparator_2_eq, comparator_3_eq, comparator_4_eq;

  Comparator_part #(.width(4)) comparator_1 (.a(4'b0010), .b(PC_Next), .eq(comparator_1_eq));  // open: gt, lt
  Comparator_part #(.width(4)) comparator_2 (.a(4'b1010), .b(PC_Next), .eq(comparator_2_eq));  // open: gt, lt
  Comparator_part #(.width(4)) comparator_3 (.a(PC_Next), .b(4'b0001), .eq(comparator_3_eq));  // open: gt, lt
  Comparator_part #(.width(20)) comparator_4 (.a(PC_In), .b(PC_Out), .eq(comparator_4_eq));  // open: gt, lt
  and and_1 (and_1_out, Branch, comparator_4_eq);
  or or_1 (No_Operation, comparator_1_eq, comparator_2_eq, comparator_3_eq, and_1_out);
endmodule

module WB_OPeration_detect (
  input  [31:0] RS,
  input  H,
  input  [31:0] RT,
  input  L,
  input  [31:0] WB_OUT,
  output [31:0] RS_2,
  output [31:0] RT_2
);

  Multiplexer #(.width(32)) multiplexer_1 (.in0(RS), .in1(WB_OUT), .out(RS_2), .sel(H));  // open: en
  Multiplexer #(.width(32)) multiplexer_2 (.in0(RT), .in1(WB_OUT), .out(RT_2), .sel(L));  // open: en
endmodule

module LW_Hazard_Detect (
  input  in_1,
  input  [2:0] Rd_IF_ID,
  input  IsLW,
  input  [2:0] Rd_ID_EX,
  input  [2:0] Rs_IF_ID,
  output FlushID,
  output StallIF,
  output StallID,
  output Flush_Select
);

  wire comparator_1_eq, comparator_2_eq, d_ff_1_q, or_1_out;

  Comparator_part #(.width(3)) comparator_1 (.a(Rd_IF_ID), .b(Rd_ID_EX), .eq(comparator_1_eq));  // open: gt, lt
  Comparator_part #(.width(3)) comparator_2 (.a(Rd_ID_EX), .b(Rs_IF_ID), .eq(comparator_2_eq));  // open: gt, lt
  or or_1 (or_1_out, comparator_1_eq, comparator_2_eq);
  and and_1 (Flush_Select, IsLW, or_1_out);
  and and_2 (FlushID, in_1, d_ff_1_q);
  D_Flip_Flop #(.trigger("falling")) d_ff_1 (
    .clk(in_1), .D(Flush_Select), .Q(d_ff_1_q));  // open: Qn, preset, en, reset

  assign StallID = Flush_Select;
  assign StallIF = Flush_Select;

  // Notes on the sheet:
  //   hasHazard
endmodule

module Comparator (
  input  [31:0] RS_DATA,
  input  [31:0] RD_DATA,
  output Bne,
  output Beq,
  output BNEZ,
  output BEQZ,
  output BQTZ,
  output BLTZ,
  output BGEZ,
  output BLEZ
);

  Comparator_part #(.width(32)) comparator_1 (.a(RS_DATA), .b(RD_DATA), .eq(Beq));  // open: gt, lt
  Comparator_part #(.width(32)) comparator_2 (.a(RD_DATA), .b({32{1'b0}}), .gt(BQTZ), .eq(BEQZ), .lt(BLTZ));
  not not_1 (Bne, Beq);
  not not_2 (BNEZ, BEQZ);
  not not_3 (BGEZ, BLTZ);
  not not_4 (BLEZ, BQTZ);
endmodule

// IF/ ID
module IF_ID (
  input  [19:0] Next_Pc_ID,
  input  [15:0] Instruction_ID,
  input  Clear,
  input  CLK,
  input  en,
  output [19:0] Next_Pc_IF,
  output [15:0] Instruction_IF
);

  Register #(.width(20)) PC (.D(Next_Pc_ID), .en(en), .Q(Next_Pc_IF), .clk(CLK), .clr(Clear));
  Register #(.width(16)) Instruction (.D(Instruction_ID), .en(en), .Q(Instruction_IF), .clk(CLK), .clr(Clear));
endmodule

module ID_EX (
  input  [25:0] Control_ID,
  input  [19:0] PC_Next_ID,
  input  [4:0] _5_bit_Imm_ID,
  input  [31:0] Bus_A_ID,
  input  [31:0] Bus_B_ID,
  input  [31:0] Bus_D_ID,
  input  [2:0] RT_ID,
  input  [2:0] RS_ID,
  input  [2:0] RD_ID,
  input  [7:0] _8_Imm,
  input  [31:0] PC_2,
  input  [4:0] Opcode_ID_Ex,
  input  CLK,
  input  in_14,
  output [3:0] alu_op_1,
  output en_1,
  output [1:0] regdest_1,
  output re_wr_1,
  output alu_src_1,
  output mem_write_1,
  output mem_read_1,
  output [1:0] mem_to_reg_1,
  output [3:0] pc_next_1,
  output branch_1,
  output c_in_1,
  output [19:0] PC_Next_Ex,
  output [1:0] shift_select_1,
  output rt___rd_1,
  output imm_in_1,
  output [4:0] _5_bit_Imm_EX,
  output set___sset_1,
  output [1:0] imm_selctor_1,
  output [31:0] Bus_A_EX,
  output [31:0] Bus_B_EX,
  output [31:0] Bus_D_EX,
  output [2:0] RT_Ex,
  output [2:0] RS_EX,
  output [2:0] RD_EX,
  output [7:0] _8_Imm_2,
  output [31:0] PC_2_2,
  output [4:0] Opcode_EX_MEM
);

  Register #(.width(26)) PC (
    .D(Control_ID), .en(1'b1),
    .Q({imm_selctor_1, set___sset_1, imm_in_1, rt___rd_1, shift_select_1, c_in_1, branch_1, pc_next_1, mem_to_reg_1, mem_read_1, mem_write_1, alu_src_1, re_wr_1, regdest_1, en_1, alu_op_1}),
    .clk(CLK), .clr(in_14));
  Register #(.width(20)) u_PC_2 (.D(PC_Next_ID), .en(1'b1), .Q(PC_Next_Ex), .clk(CLK), .clr(in_14));
  Register #(.width(5)) Imm (.D(_5_bit_Imm_ID), .en(1'b1), .Q(_5_bit_Imm_EX), .clk(CLK), .clr(in_14));
  Register #(.width(32)) Bus_A (.D(Bus_A_ID), .en(1'b1), .Q(Bus_A_EX), .clk(CLK), .clr(in_14));
  Register #(.width(32)) Bus_B (.D(Bus_B_ID), .en(1'b1), .Q(Bus_B_EX), .clk(CLK), .clr(in_14));
  Register #(.width(32)) Bus_D (.D(Bus_D_ID), .en(1'b1), .Q(Bus_D_EX), .clk(CLK), .clr(in_14));
  Register #(.width(3)) RT (.D(RT_ID), .en(1'b1), .Q(RT_Ex), .clk(CLK), .clr(in_14));
  Register #(.width(3)) RS (.D(RS_ID), .en(1'b1), .Q(RS_EX), .clk(CLK), .clr(in_14));
  Register #(.width(3)) RD (.D(RD_ID), .en(1'b1), .Q(RD_EX), .clk(CLK), .clr(in_14));
  Register u__8_Imm (.D(_8_Imm), .en(1'b1), .Q(_8_Imm_2), .clk(CLK), .clr(in_14));
  Register #(.width(32)) u_PC_2_dup2 (.D(PC_2), .en(1'b1), .Q(PC_2_2), .clk(CLK), .clr(in_14));
  Register #(.width(5)) Op_Code (.D(Opcode_ID_Ex), .en(1'b1), .Q(Opcode_EX_MEM), .clk(CLK), .clr(in_14));
endmodule

module EX_MEM (
  input  re_write1,
  input  Mem_Write_1,
  input  Mem_Read_1,
  input  [1:0] Mem_to_reg_1,
  input  [31:0] ALU_EX,
  input  [31:0] Memory_Data_EX,
  input  [2:0] RD_EX,
  input  [31:0] PC_2,
  input  CLK,
  output re_write_2,
  output Mem_Write_2,
  output Mem_Read_2,
  output [1:0] Mem_to_reg_1_2,
  output [31:0] ALU_MEM,
  output [31:0] Memory_Data_MEM,
  output [2:0] RD_MEM,
  output [31:0] PC_2_2
);

  Register #(.width(1)) register_1 (.D(re_write1), .en(1'b1), .Q(re_write_2), .clk(CLK), .clr(1'b0));
  Register #(.width(1)) register_2 (.D(Mem_Write_1), .en(1'b1), .Q(Mem_Write_2), .clk(CLK), .clr(1'b0));
  Register #(.width(1)) register_3 (.D(Mem_Read_1), .en(1'b1), .Q(Mem_Read_2), .clk(CLK), .clr(1'b0));
  Register #(.width(2)) register_4 (.D(Mem_to_reg_1), .en(1'b1), .Q(Mem_to_reg_1_2), .clk(CLK), .clr(1'b0));
  Register #(.width(32)) ALU_output (.D(ALU_EX), .en(1'b1), .Q(ALU_MEM), .clk(CLK), .clr(1'b0));
  Register #(.width(32)) Memory_Data (.D(Memory_Data_EX), .en(1'b1), .Q(Memory_Data_MEM), .clk(CLK), .clr(1'b0));
  Register #(.width(3)) RD (.D(RD_EX), .en(1'b1), .Q(RD_MEM), .clk(CLK), .clr(1'b0));
  Register #(.width(32)) u_PC_2 (.D(PC_2), .en(1'b1), .Q(PC_2_2), .clk(CLK), .clr(1'b0));
endmodule

module MEM_WB (
  input  re_write_2,
  input  [1:0] Mem_to_Reg_2,
  input  [31:0] ALU_out_MEM,
  input  [31:0] Memory_Data_MEM,
  input  [2:0] RD_MEM,
  input  [31:0] Rd_Mem_2,
  input  [31:0] PC_2,
  input  CLK,
  output re_write_3,
  output [1:0] Mem_to_Reg_3,
  output [31:0] ALU_Out_WB,
  output [31:0] Memory_Data_WB,
  output [2:0] RD_WB,
  output [31:0] RD_WB_2,
  output [31:0] PC_2_2
);

  Register #(.width(1)) register_1 (.D(re_write_2), .en(1'b1), .Q(re_write_3), .clk(CLK), .clr(1'b0));
  Register #(.width(2)) register_2 (.D(Mem_to_Reg_2), .en(1'b1), .Q(Mem_to_Reg_3), .clk(CLK), .clr(1'b0));
  Register #(.width(32)) ALU_output (.D(ALU_out_MEM), .en(1'b1), .Q(ALU_Out_WB), .clk(CLK), .clr(1'b0));
  Register #(.width(32)) Memory_Data (.D(Memory_Data_MEM), .en(1'b1), .Q(Memory_Data_WB), .clk(CLK), .clr(1'b0));
  Register #(.width(3)) RD (.D(RD_MEM), .en(1'b1), .Q(RD_WB), .clk(CLK), .clr(1'b0));
  Register #(.width(32)) RD___data (.D(Rd_Mem_2), .en(1'b1), .Q(RD_WB_2), .clk(CLK), .clr(1'b0));
  Register #(.width(32)) u_PC_2 (.D(PC_2), .en(1'b1), .Q(PC_2_2), .clk(CLK), .clr(1'b0));
endmodule

module \and  (
  output [3:0] alu_op,
  output en,
  output [1:0] regdest,
  output re_wr,
  output alu_src,
  output mem_write,
  output mem_read,
  output [1:0] mem_to_reg,
  output [3:0] pc_next,
  output branch,
  output c_in,
  output [1:0] shift_select,
  output rt___rd,
  output imm_in,
  output set___sset,
  output [1:0] imm_selctor
);


  assign alu_op = 4'b0000;
  assign alu_src = 1'b0;
  assign branch = 1'b0;
  assign c_in = 1'b0;
  assign en = 1'b1;
  assign imm_in = 1'b0;
  assign imm_selctor = 2'b00;
  assign mem_read = 1'b0;
  assign mem_to_reg = 2'b00;
  assign mem_write = 1'b0;
  assign pc_next = 4'b0000;
  assign re_wr = 1'b1;
  assign regdest = 2'b01;
  assign rt___rd = 1'b0;
  assign set___sset = 1'b0;
  assign shift_select = 2'b00;
endmodule

module \or  (
  output [3:0] alu_op,
  output en,
  output [1:0] regdest,
  output re_wr,
  output alu_src,
  output mem_write,
  output mem_read,
  output [1:0] mem_to_reg,
  output [3:0] pc_next,
  output branch,
  output c_in,
  output [1:0] shift_select,
  output rt___rd,
  output imm_in,
  output set___sset,
  output [1:0] imm_selctor
);


  assign alu_op = 4'b0001;
  assign alu_src = 1'b0;
  assign branch = 1'b0;
  assign c_in = 1'b0;
  assign en = 1'b1;
  assign imm_in = 1'b0;
  assign imm_selctor = 2'b00;
  assign mem_read = 1'b0;
  assign mem_to_reg = 2'b00;
  assign mem_write = 1'b0;
  assign pc_next = 4'b0000;
  assign re_wr = 1'b1;
  assign regdest = 2'b01;
  assign rt___rd = 1'b0;
  assign set___sset = 1'b0;
  assign shift_select = 2'b00;
endmodule

module \xor  (
  output [3:0] alu_op,
  output en,
  output [1:0] regdest,
  output re_wr,
  output alu_src,
  output mem_write,
  output mem_read,
  output [1:0] mem_to_reg,
  output [3:0] pc_next,
  output branch,
  output c_in,
  output [1:0] shift_select,
  output rt___rd,
  output imm_in,
  output set___sset,
  output [1:0] imm_selctor
);


  assign alu_op = 4'b0010;
  assign alu_src = 1'b0;
  assign branch = 1'b0;
  assign c_in = 1'b0;
  assign en = 1'b1;
  assign imm_in = 1'b0;
  assign imm_selctor = 2'b00;
  assign mem_read = 1'b0;
  assign mem_to_reg = 2'b00;
  assign mem_write = 1'b0;
  assign pc_next = 4'b0000;
  assign re_wr = 1'b1;
  assign regdest = 2'b01;
  assign rt___rd = 1'b0;
  assign set___sset = 1'b0;
  assign shift_select = 2'b00;
endmodule

module eqv (
  output [3:0] alu_op,
  output en,
  output [1:0] regdest,
  output re_wr,
  output alu_src,
  output mem_write,
  output mem_read,
  output [1:0] mem_to_reg,
  output [3:0] pc_next,
  output branch,
  output c_in,
  output [1:0] shift_select,
  output rt___rd,
  output imm_in,
  output set___sset,
  output [1:0] imm_selctor
);


  assign alu_op = 4'b0100;
  assign alu_src = 1'b0;
  assign branch = 1'b0;
  assign c_in = 1'b0;
  assign en = 1'b1;
  assign imm_in = 1'b0;
  assign imm_selctor = 2'b00;
  assign mem_read = 1'b0;
  assign mem_to_reg = 2'b00;
  assign mem_write = 1'b0;
  assign pc_next = 4'b0000;
  assign re_wr = 1'b1;
  assign regdest = 2'b01;
  assign rt___rd = 1'b0;
  assign set___sset = 1'b0;
  assign shift_select = 2'b00;
endmodule

module add (
  output [3:0] alu_op,
  output en,
  output [1:0] regdest,
  output re_wr,
  output alu_src,
  output mem_write,
  output mem_read,
  output [1:0] mem_to_reg,
  output [3:0] pc_next,
  output branch,
  output c_in,
  output [1:0] shift_select,
  output rt___rd,
  output imm_in,
  output set___sset,
  output [1:0] imm_selctor
);


  assign alu_op = 4'b0011;
  assign alu_src = 1'b0;
  assign branch = 1'b0;
  assign c_in = 1'b0;
  assign en = 1'b1;
  assign imm_in = 1'b0;
  assign imm_selctor = 2'b00;
  assign mem_read = 1'b0;
  assign mem_to_reg = 2'b00;
  assign mem_write = 1'b0;
  assign pc_next = 4'b0000;
  assign re_wr = 1'b1;
  assign regdest = 2'b01;
  assign rt___rd = 1'b0;
  assign set___sset = 1'b0;
  assign shift_select = 2'b00;
endmodule

module sub (
  output [3:0] alu_op,
  output en,
  output [1:0] regdest,
  output re_wr,
  output alu_src,
  output mem_write,
  output mem_read,
  output [1:0] mem_to_reg,
  output [3:0] pc_next,
  output branch,
  output c_in,
  output [1:0] shift_select,
  output rt___rd,
  output imm_in,
  output set___sset,
  output [1:0] imm_selctor
);


  assign alu_op = 4'b0011;
  assign alu_src = 1'b0;
  assign branch = 1'b0;
  assign c_in = 1'b1;
  assign en = 1'b1;
  assign imm_in = 1'b0;
  assign imm_selctor = 2'b00;
  assign mem_read = 1'b0;
  assign mem_to_reg = 2'b00;
  assign mem_write = 1'b0;
  assign pc_next = 4'b0000;
  assign re_wr = 1'b1;
  assign regdest = 2'b01;
  assign rt___rd = 1'b0;
  assign set___sset = 1'b0;
  assign shift_select = 2'b00;
endmodule

module slt (
  output [3:0] alu_op,
  output en,
  output [1:0] regdest,
  output re_wr,
  output alu_src,
  output mem_write,
  output mem_read,
  output [1:0] mem_to_reg,
  output [3:0] pc_next,
  output branch,
  output c_in,
  output [1:0] shift_select,
  output rt___rd,
  output imm_in,
  output set___sset,
  output [1:0] imm_selctor
);


  assign alu_op = 4'b0111;
  assign alu_src = 1'b0;
  assign branch = 1'b0;
  assign c_in = 1'b0;
  assign en = 1'b1;
  assign imm_in = 1'b0;
  assign imm_selctor = 2'b00;
  assign mem_read = 1'b0;
  assign mem_to_reg = 2'b00;
  assign mem_write = 1'b0;
  assign pc_next = 4'b0000;
  assign re_wr = 1'b1;
  assign regdest = 2'b01;
  assign rt___rd = 1'b0;
  assign set___sset = 1'b0;
  assign shift_select = 2'b00;
endmodule

module seq (
  output [3:0] alu_op,
  output en,
  output [1:0] regdest,
  output re_wr,
  output alu_src,
  output mem_write,
  output mem_read,
  output [1:0] mem_to_reg,
  output [3:0] pc_next,
  output branch,
  output c_in,
  output [1:0] shift_select,
  output rt___rd,
  output imm_in,
  output set___sset,
  output [1:0] imm_selctor
);


  assign alu_op = 4'b1000;
  assign alu_src = 1'b0;
  assign branch = 1'b0;
  assign c_in = 1'b0;
  assign en = 1'b1;
  assign imm_in = 1'b0;
  assign imm_selctor = 2'b00;
  assign mem_read = 1'b0;
  assign mem_to_reg = 2'b00;
  assign mem_write = 1'b0;
  assign pc_next = 4'b0000;
  assign re_wr = 1'b1;
  assign regdest = 2'b01;
  assign rt___rd = 1'b0;
  assign set___sset = 1'b0;
  assign shift_select = 2'b00;
endmodule

module andi (
  output [3:0] alu_op,
  output en,
  output [1:0] regdest,
  output re_wr,
  output alu_src,
  output mem_write,
  output mem_read,
  output [1:0] mem_to_reg,
  output [3:0] pc_next,
  output branch,
  output c_in,
  output [1:0] shift_select,
  output rt___rd,
  output imm_in,
  output set___sset,
  output [1:0] imm_selctor
);


  assign alu_op = 4'b0000;
  assign alu_src = 1'b1;
  assign branch = 1'b0;
  assign c_in = 1'b0;
  assign en = 1'b1;
  assign imm_in = 1'b0;
  assign imm_selctor = 2'b00;
  assign mem_read = 1'b0;
  assign mem_to_reg = 2'b00;
  assign mem_write = 1'b0;
  assign pc_next = 4'b0000;
  assign re_wr = 1'b1;
  assign regdest = 2'b00;
  assign rt___rd = 1'b0;
  assign set___sset = 1'b0;
  assign shift_select = 2'b00;
endmodule

module ori (
  output [3:0] alu_op,
  output en,
  output [1:0] regdest,
  output re_wr,
  output alu_src,
  output mem_write,
  output mem_read,
  output [1:0] mem_to_reg,
  output [3:0] pc_next,
  output branch,
  output c_in,
  output [1:0] shift_select,
  output rt___rd,
  output imm_in,
  output set___sset,
  output [1:0] imm_selctor
);


  assign alu_op = 4'b0001;
  assign alu_src = 1'b1;
  assign branch = 1'b0;
  assign c_in = 1'b0;
  assign en = 1'b1;
  assign imm_in = 1'b0;
  assign imm_selctor = 2'b00;
  assign mem_read = 1'b0;
  assign mem_to_reg = 2'b00;
  assign mem_write = 1'b0;
  assign pc_next = 4'b0000;
  assign re_wr = 1'b1;
  assign regdest = 2'b00;
  assign rt___rd = 1'b0;
  assign set___sset = 1'b0;
  assign shift_select = 2'b00;
endmodule

module xori (
  output [3:0] alu_op,
  output en,
  output [1:0] regdest,
  output re_wr,
  output alu_src,
  output mem_write,
  output mem_read,
  output [1:0] mem_to_reg,
  output [3:0] pc_next,
  output branch,
  output c_in,
  output [1:0] shift_select,
  output rt___rd,
  output imm_in,
  output set___sset,
  output [1:0] imm_selctor
);


  assign alu_op = 4'b0010;
  assign alu_src = 1'b1;
  assign branch = 1'b0;
  assign c_in = 1'b0;
  assign en = 1'b1;
  assign imm_in = 1'b0;
  assign imm_selctor = 2'b00;
  assign mem_read = 1'b0;
  assign mem_to_reg = 2'b00;
  assign mem_write = 1'b0;
  assign pc_next = 4'b0000;
  assign re_wr = 1'b1;
  assign regdest = 2'b00;
  assign rt___rd = 1'b0;
  assign set___sset = 1'b0;
  assign shift_select = 2'b00;
endmodule

module eqvi (
  output [3:0] alu_op,
  output en,
  output [1:0] regdest,
  output re_wr,
  output alu_src,
  output mem_write,
  output mem_read,
  output [1:0] mem_to_reg,
  output [3:0] pc_next,
  output branch,
  output c_in,
  output [1:0] shift_select,
  output rt___rd,
  output imm_in,
  output set___sset,
  output [1:0] imm_selctor
);


  assign alu_op = 4'b0100;
  assign alu_src = 1'b1;
  assign branch = 1'b0;
  assign c_in = 1'b0;
  assign en = 1'b1;
  assign imm_in = 1'b0;
  assign imm_selctor = 2'b00;
  assign mem_read = 1'b0;
  assign mem_to_reg = 2'b00;
  assign mem_write = 1'b0;
  assign pc_next = 4'b0000;
  assign re_wr = 1'b1;
  assign regdest = 2'b00;
  assign rt___rd = 1'b0;
  assign set___sset = 1'b0;
  assign shift_select = 2'b00;
endmodule

module addi (
  output [3:0] alu_op,
  output en,
  output [1:0] regdest,
  output re_wr,
  output alu_src,
  output mem_write,
  output mem_read,
  output [1:0] mem_to_reg,
  output [3:0] pc_next,
  output branch,
  output c_in,
  output [1:0] shift_select,
  output rt___rd,
  output imm_in,
  output set___sset,
  output [1:0] imm_selctor
);


  assign alu_op = 4'b0011;
  assign alu_src = 1'b1;
  assign branch = 1'b0;
  assign c_in = 1'b0;
  assign en = 1'b1;
  assign imm_in = 1'b0;
  assign imm_selctor = 2'b10;
  assign mem_read = 1'b0;
  assign mem_to_reg = 2'b00;
  assign mem_write = 1'b0;
  assign pc_next = 4'b0000;
  assign re_wr = 1'b1;
  assign regdest = 2'b00;
  assign rt___rd = 1'b0;
  assign set___sset = 1'b0;
  assign shift_select = 2'b00;
endmodule

module slti (
  output [3:0] alu_op,
  output en,
  output [1:0] regdest,
  output re_wr,
  output alu_src,
  output mem_write,
  output mem_read,
  output [1:0] mem_to_reg,
  output [3:0] pc_next,
  output branch,
  output c_in,
  output [1:0] shift_select,
  output rt___rd,
  output imm_in,
  output set___sset,
  output [1:0] imm_selctor
);


  assign alu_op = 4'b0111;
  assign alu_src = 1'b1;
  assign branch = 1'b0;
  assign c_in = 1'b0;
  assign en = 1'b1;
  assign imm_in = 1'b0;
  assign imm_selctor = 2'b10;
  assign mem_read = 1'b0;
  assign mem_to_reg = 2'b00;
  assign mem_write = 1'b0;
  assign pc_next = 4'b0000;
  assign re_wr = 1'b1;
  assign regdest = 2'b00;
  assign rt___rd = 1'b0;
  assign set___sset = 1'b0;
  assign shift_select = 2'b00;
endmodule

module seqi (
  output [3:0] alu_op,
  output en,
  output [1:0] regdest,
  output re_wr,
  output alu_src,
  output mem_write,
  output mem_read,
  output [1:0] mem_to_reg,
  output [3:0] pc_next,
  output branch,
  output c_in,
  output [1:0] shift_select,
  output rt___rd,
  output imm_in,
  output set___sset,
  output [1:0] imm_selctor
);


  assign alu_op = 4'b1000;
  assign alu_src = 1'b1;
  assign branch = 1'b0;
  assign c_in = 1'b0;
  assign en = 1'b1;
  assign imm_in = 1'b0;
  assign imm_selctor = 2'b10;
  assign mem_read = 1'b0;
  assign mem_to_reg = 2'b00;
  assign mem_write = 1'b0;
  assign pc_next = 4'b0000;
  assign re_wr = 1'b1;
  assign regdest = 2'b00;
  assign rt___rd = 1'b0;
  assign set___sset = 1'b0;
  assign shift_select = 2'b00;
endmodule

module sll (
  output [3:0] alu_op,
  output en,
  output [1:0] regdest,
  output re_wr,
  output alu_src,
  output mem_write,
  output mem_read,
  output [1:0] mem_to_reg,
  output [3:0] pc_next,
  output branch,
  output c_in,
  output [1:0] shift_select,
  output rt___rd,
  output imm_in,
  output set___sset,
  output [1:0] imm_selctor
);


  assign alu_op = 4'b0101;
  assign alu_src = 1'b1;
  assign branch = 1'b0;
  assign c_in = 1'b0;
  assign en = 1'b1;
  assign imm_in = 1'b0;
  assign imm_selctor = 2'b00;
  assign mem_read = 1'b0;
  assign mem_to_reg = 2'b00;
  assign mem_write = 1'b0;
  assign pc_next = 4'b0000;
  assign re_wr = 1'b1;
  assign regdest = 2'b00;
  assign rt___rd = 1'b0;
  assign set___sset = 1'b0;
  assign shift_select = 2'b00;
endmodule

module srl (
  output [3:0] alu_op,
  output en,
  output [1:0] regdest,
  output re_wr,
  output alu_src,
  output mem_write,
  output mem_read,
  output [1:0] mem_to_reg,
  output [3:0] pc_next,
  output branch,
  output c_in,
  output [1:0] shift_select,
  output rt___rd,
  output imm_in,
  output set___sset,
  output [1:0] imm_selctor
);


  assign alu_op = 4'b0101;
  assign alu_src = 1'b1;
  assign branch = 1'b0;
  assign c_in = 1'b0;
  assign en = 1'b1;
  assign imm_in = 1'b0;
  assign imm_selctor = 2'b00;
  assign mem_read = 1'b0;
  assign mem_to_reg = 2'b00;
  assign mem_write = 1'b0;
  assign pc_next = 4'b0000;
  assign re_wr = 1'b1;
  assign regdest = 2'b00;
  assign rt___rd = 1'b0;
  assign set___sset = 1'b0;
  assign shift_select = 2'b01;
endmodule

module ror (
  output [3:0] alu_op,
  output en,
  output [1:0] regdest,
  output re_wr,
  output alu_src,
  output mem_write,
  output mem_read,
  output [1:0] mem_to_reg,
  output [3:0] pc_next,
  output branch,
  output c_in,
  output [1:0] shift_select,
  output rt___rd,
  output imm_in,
  output set___sset,
  output [1:0] imm_selctor
);


  assign alu_op = 4'b0101;
  assign alu_src = 1'b1;
  assign branch = 1'b0;
  assign c_in = 1'b0;
  assign en = 1'b1;
  assign imm_in = 1'b0;
  assign imm_selctor = 2'b10;
  assign mem_read = 1'b0;
  assign mem_to_reg = 2'b00;
  assign mem_write = 1'b0;
  assign pc_next = 4'b0000;
  assign re_wr = 1'b1;
  assign regdest = 2'b00;
  assign rt___rd = 1'b0;
  assign set___sset = 1'b0;
  assign shift_select = 2'b11;
endmodule

module beq (
  output [3:0] alu_op,
  output en,
  output [1:0] regdest,
  output re_wr,
  output alu_src,
  output mem_write,
  output mem_read,
  output [1:0] mem_to_reg,
  output [3:0] pc_next,
  output branch,
  output c_in,
  output [1:0] shift_select,
  output rt___rd,
  output imm_in,
  output set___sset,
  output [1:0] imm_selctor
);


  assign alu_op = 4'b0000;
  assign alu_src = 1'b0;
  assign branch = 1'b1;
  assign c_in = 1'b0;
  assign en = 1'b1;
  assign imm_in = 1'b0;
  assign imm_selctor = 2'b00;
  assign mem_read = 1'b0;
  assign mem_to_reg = 2'b00;
  assign mem_write = 1'b0;
  assign pc_next = 4'b0000;
  assign re_wr = 1'b0;
  assign regdest = 2'b00;
  assign rt___rd = 1'b1;
  assign set___sset = 1'b0;
  assign shift_select = 2'b00;
endmodule

module bnq (
  output [3:0] alu_op,
  output en,
  output [1:0] regdest,
  output re_wr,
  output alu_src,
  output mem_write,
  output mem_read,
  output [1:0] mem_to_reg,
  output [3:0] pc_next,
  output branch,
  output c_in,
  output [1:0] shift_select,
  output rt___rd,
  output imm_in,
  output set___sset,
  output [1:0] imm_selctor
);


  assign alu_op = 4'b0000;
  assign alu_src = 1'b0;
  assign branch = 1'b1;
  assign c_in = 1'b0;
  assign en = 1'b1;
  assign imm_in = 1'b0;
  assign imm_selctor = 2'b00;
  assign mem_read = 1'b0;
  assign mem_to_reg = 2'b00;
  assign mem_write = 1'b0;
  assign pc_next = 4'b0011;
  assign re_wr = 1'b0;
  assign regdest = 2'b00;
  assign rt___rd = 1'b1;
  assign set___sset = 1'b0;
  assign shift_select = 2'b00;
endmodule

module lw (
  output [3:0] alu_op,
  output en,
  output [1:0] regdest,
  output re_wr,
  output alu_src,
  output mem_write,
  output mem_read,
  output [1:0] mem_to_reg,
  output [3:0] pc_next,
  output branch,
  output c_in,
  output [1:0] shift_select,
  output rt___rd,
  output imm_in,
  output set___sset,
  output [1:0] imm_selctor
);


  assign alu_op = 4'b0011;
  assign alu_src = 1'b1;
  assign branch = 1'b0;
  assign c_in = 1'b0;
  assign en = 1'b1;
  assign imm_in = 1'b0;
  assign imm_selctor = 2'b01;
  assign mem_read = 1'b1;
  assign mem_to_reg = 2'b01;
  assign mem_write = 1'b0;
  assign pc_next = 4'b1110;
  assign re_wr = 1'b1;
  assign regdest = 2'b00;
  assign rt___rd = 1'b0;
  assign set___sset = 1'b0;
  assign shift_select = 2'b00;
endmodule

module sw (
  output [3:0] alu_op,
  output en,
  output [1:0] regdest,
  output re_wr,
  output alu_src,
  output mem_write,
  output mem_read,
  output [1:0] mem_to_reg,
  output [3:0] pc_next,
  output branch,
  output c_in,
  output [1:0] shift_select,
  output rt___rd,
  output imm_in,
  output set___sset,
  output [1:0] imm_selctor
);


  assign alu_op = 4'b0011;
  assign alu_src = 1'b1;
  assign branch = 1'b0;
  assign c_in = 1'b0;
  assign en = 1'b1;
  assign imm_in = 1'b0;
  assign imm_selctor = 2'b01;
  assign mem_read = 1'b0;
  assign mem_to_reg = 2'b10;
  assign mem_write = 1'b1;
  assign pc_next = 4'b1110;
  assign re_wr = 1'b1;
  assign regdest = 2'b00;
  assign rt___rd = 1'b0;
  assign set___sset = 1'b0;
  assign shift_select = 2'b00;
endmodule

module Beqz (
  output [3:0] alu_op,
  output en,
  output [1:0] regdest,
  output re_wr,
  output alu_src,
  output mem_write,
  output mem_read,
  output [1:0] mem_to_reg,
  output [3:0] pc_next,
  output branch,
  output c_in,
  output [1:0] shift_select,
  output rt___rd,
  output imm_in,
  output set___sset,
  output [1:0] imm_selctor
);


  assign alu_op = 4'b0000;
  assign alu_src = 1'b0;
  assign branch = 1'b1;
  assign c_in = 1'b0;
  assign en = 1'b1;
  assign imm_in = 1'b1;
  assign imm_selctor = 2'b00;
  assign mem_read = 1'b0;
  assign mem_to_reg = 2'b00;
  assign mem_write = 1'b0;
  assign pc_next = 4'b0100;
  assign re_wr = 1'b0;
  assign regdest = 2'b00;
  assign rt___rd = 1'b1;
  assign set___sset = 1'b0;
  assign shift_select = 2'b00;
endmodule

module Bnez (
  output [3:0] alu_op,
  output en,
  output [1:0] regdest,
  output re_wr,
  output alu_src,
  output mem_write,
  output mem_read,
  output [1:0] mem_to_reg,
  output [3:0] out_9,
  output branch,
  output c_in,
  output [1:0] shift_select,
  output rt___rd,
  output imm_in,
  output set___sset,
  output [1:0] imm_selctor
);


  assign alu_op = 4'b0000;
  assign alu_src = 1'b0;
  assign branch = 1'b1;
  assign c_in = 1'b0;
  assign en = 1'b1;
  assign imm_in = 1'b1;
  assign imm_selctor = 2'b00;
  assign mem_read = 1'b0;
  assign mem_to_reg = 2'b00;
  assign mem_write = 1'b0;
  assign out_9 = 4'b0101;
  assign re_wr = 1'b0;
  assign regdest = 2'b00;
  assign rt___rd = 1'b1;
  assign set___sset = 1'b0;
  assign shift_select = 2'b00;
endmodule

module Bltz (
  output [3:0] alu_op,
  output en,
  output [1:0] regdest,
  output re_wr,
  output alu_src,
  output mem_write,
  output mem_read,
  output [1:0] mem_to_reg,
  output [3:0] pc_next,
  output branch,
  output c_in,
  output [1:0] shift_select,
  output rt___rd,
  output imm_in,
  output set___sset,
  output [1:0] imm_selctor
);


  assign alu_op = 4'b0000;
  assign alu_src = 1'b0;
  assign branch = 1'b1;
  assign c_in = 1'b0;
  assign en = 1'b1;
  assign imm_in = 1'b1;
  assign imm_selctor = 2'b00;
  assign mem_read = 1'b0;
  assign mem_to_reg = 2'b00;
  assign mem_write = 1'b0;
  assign pc_next = 4'b0110;
  assign re_wr = 1'b0;
  assign regdest = 2'b00;
  assign rt___rd = 1'b1;
  assign set___sset = 1'b0;
  assign shift_select = 2'b00;

  // Notes on the sheet:
  //   pc_next: pull=up
endmodule

module Bgez (
  output [3:0] alu_op,
  output en,
  output [1:0] regdest,
  output re_wr,
  output alu_src,
  output mem_write,
  output mem_read,
  output [1:0] mem_to_reg,
  output [3:0] pc_next,
  output branch,
  output c_in,
  output [1:0] shift_select,
  output rt___rd,
  output imm_in,
  output set___sset,
  output [1:0] imm_selctor
);


  assign alu_op = 4'b0000;
  assign alu_src = 1'b0;
  assign branch = 1'b1;
  assign c_in = 1'b0;
  assign en = 1'b1;
  assign imm_in = 1'b1;
  assign imm_selctor = 2'b00;
  assign mem_read = 1'b0;
  assign mem_to_reg = 2'b00;
  assign mem_write = 1'b0;
  assign pc_next = 4'b0111;
  assign re_wr = 1'b0;
  assign regdest = 2'b00;
  assign rt___rd = 1'b1;
  assign set___sset = 1'b0;
  assign shift_select = 2'b00;

  // Notes on the sheet:
  //   pc_next: pull=up
endmodule

module Bjtz (
  output [3:0] alu_op,
  output en,
  output [1:0] regdest,
  output re_wr,
  output alu_src,
  output mem_write,
  output mem_read,
  output [1:0] mem_to_reg,
  output [3:0] pc_next,
  output branch,
  output c_in,
  output [1:0] shift_select,
  output rt___rd,
  output imm_in,
  output set___sset,
  output [1:0] imm_selctor
);


  assign alu_op = 4'b0000;
  assign alu_src = 1'b0;
  assign branch = 1'b1;
  assign c_in = 1'b0;
  assign en = 1'b1;
  assign imm_in = 1'b1;
  assign imm_selctor = 2'b00;
  assign mem_read = 1'b0;
  assign mem_to_reg = 2'b00;
  assign mem_write = 1'b0;
  assign pc_next = 4'b1000;
  assign re_wr = 1'b0;
  assign regdest = 2'b00;
  assign rt___rd = 1'b1;
  assign set___sset = 1'b0;
  assign shift_select = 2'b00;

  // Notes on the sheet:
  //   pc_next: pull=up
endmodule

module Blez (
  output [3:0] alu_op,
  output en,
  output [1:0] regdest,
  output re_wr,
  output alu_src,
  output mem_write,
  output mem_read,
  output [1:0] mem_to_reg,
  output [3:0] pc_next,
  output branch,
  output c_in,
  output [1:0] shift_select,
  output rt___rd,
  output imm_in,
  output set___sset,
  output [1:0] imm_selctor
);


  assign alu_op = 4'b0000;
  assign alu_src = 1'b0;
  assign branch = 1'b1;
  assign c_in = 1'b0;
  assign en = 1'b1;
  assign imm_in = 1'b1;
  assign imm_selctor = 2'b00;
  assign mem_read = 1'b0;
  assign mem_to_reg = 2'b00;
  assign mem_write = 1'b0;
  assign pc_next = 4'b1001;
  assign re_wr = 1'b0;
  assign regdest = 2'b00;
  assign rt___rd = 1'b1;
  assign set___sset = 1'b0;
  assign shift_select = 2'b00;

  // Notes on the sheet:
  //   pc_next: pull=up
endmodule

module JR (
  output [3:0] alu_op,
  output en,
  output [1:0] regdest,
  output re_wr,
  output alu_src,
  output mem_write,
  output mem_read,
  output [1:0] mem_to_reg,
  output [3:0] pc_next,
  output branch,
  output c_in,
  output [1:0] shift_select,
  output rt___rd,
  output imm_in,
  output set___sset,
  output [1:0] imm_selctor
);


  assign alu_op = 4'b0101;
  assign alu_src = 1'b0;
  assign branch = 1'b0;
  assign c_in = 1'b0;
  assign en = 1'b1;
  assign imm_in = 1'b1;
  assign imm_selctor = 2'b00;
  assign mem_read = 1'b0;
  assign mem_to_reg = 2'b00;
  assign mem_write = 1'b0;
  assign pc_next = 4'b1010;
  assign re_wr = 1'b0;
  assign regdest = 2'b00;
  assign rt___rd = 1'b1;
  assign set___sset = 1'b0;
  assign shift_select = 2'b00;

  // Notes on the sheet:
  //   pc_next: pull=up
endmodule

module Jalr (
  output [3:0] alu_op,
  output en,
  output [1:0] regdest,
  output re_wr,
  output alu_src,
  output mem_write,
  output mem_read,
  output [1:0] mem_to_reg,
  output [3:0] pc_next,
  output branch,
  output c_in,
  output [1:0] shift_select,
  output rt___rd,
  output imm_in,
  output set___sset,
  output [1:0] imm_selctor
);


  assign alu_op = 4'b0000;
  assign alu_src = 1'b0;
  assign branch = 1'b0;
  assign c_in = 1'b0;
  assign en = 1'b1;
  assign imm_in = 1'b1;
  assign imm_selctor = 2'b00;
  assign mem_read = 1'b0;
  assign mem_to_reg = 2'b10;
  assign mem_write = 1'b0;
  assign pc_next = 4'b0010;
  assign re_wr = 1'b1;
  assign regdest = 2'b10;
  assign rt___rd = 1'b1;
  assign set___sset = 1'b0;
  assign shift_select = 2'b00;

  // Notes on the sheet:
  //   pc_next: pull=up
endmodule

module set (
  output [3:0] alu_op,
  output en,
  output [1:0] regdest,
  output re_wr,
  output alu_src,
  output mem_write,
  output mem_read,
  output [1:0] mem_to_reg,
  output [3:0] pc_next,
  output branch,
  output c_in,
  output [1:0] shift_select,
  output rt___rd,
  output imm_in,
  output set___sset,
  output [1:0] imm_selctor
);


  assign alu_op = 4'b1100;
  assign alu_src = 1'b1;
  assign branch = 1'b0;
  assign c_in = 1'b0;
  assign en = 1'b1;
  assign imm_in = 1'b1;
  assign imm_selctor = 2'b00;
  assign mem_read = 1'b0;
  assign mem_to_reg = 2'b00;
  assign mem_write = 1'b0;
  assign pc_next = 4'b0100;
  assign re_wr = 1'b1;
  assign regdest = 2'b00;
  assign rt___rd = 1'b1;
  assign set___sset = 1'b0;
  assign shift_select = 2'b00;

  // Notes on the sheet:
  //   pc_next: pull=up
endmodule

module SSet (
  output [3:0] alu_op,
  output en,
  output [1:0] regdest,
  output re_wr,
  output alu_src,
  output mem_write,
  output mem_read,
  output [1:0] mem_to_reg,
  output [3:0] pc_next,
  output branch,
  output c_in,
  output [1:0] shift_select,
  output rt___rd,
  output imm_in,
  output set___sset,
  output [1:0] imm_selctor
);


  assign alu_op = 4'b1011;
  assign alu_src = 1'b0;
  assign branch = 1'b0;
  assign c_in = 1'b0;
  assign en = 1'b1;
  assign imm_in = 1'b1;
  assign imm_selctor = 2'b00;
  assign mem_read = 1'b0;
  assign mem_to_reg = 2'b00;
  assign mem_write = 1'b0;
  assign pc_next = 4'b0100;
  assign re_wr = 1'b1;
  assign regdest = 2'b00;
  assign rt___rd = 1'b1;
  assign set___sset = 1'b0;
  assign shift_select = 2'b00;

  // Notes on the sheet:
  //   pc_next: pull=up
endmodule

module J (
  output [3:0] alu_op,
  output en,
  output [1:0] regdest,
  output re_wr,
  output alu_src,
  output mem_write,
  output mem_read,
  output [1:0] mem_to_reg,
  output [3:0] pc_next,
  output branch,
  output c_in,
  output [1:0] shift_select,
  output rt___rd,
  output imm_in,
  output set___sset,
  output [1:0] imm_selctor
);


  assign alu_op = 4'b0000;
  assign alu_src = 1'b0;
  assign branch = 1'b0;
  assign c_in = 1'b0;
  assign en = 1'b1;
  assign imm_in = 1'b0;
  assign imm_selctor = 2'b00;
  assign mem_read = 1'b0;
  assign mem_to_reg = 2'b00;
  assign mem_write = 1'b0;
  assign pc_next = 4'b0001;
  assign re_wr = 1'b0;
  assign regdest = 2'b00;
  assign rt___rd = 1'b0;
  assign set___sset = 1'b0;
  assign shift_select = 2'b00;
endmodule

module Jal (
  output [3:0] alu_op,
  output en,
  output [1:0] regdest,
  output re_wr,
  output alu_src,
  output mem_write,
  output mem_read,
  output [1:0] mem_to_reg,
  output [3:0] pc_next,
  output branch,
  output c_in,
  output [1:0] shift_select,
  output rt___rd,
  output imm_in,
  output set___sset,
  output [1:0] imm_selctor
);


  assign alu_op = 4'b0000;
  assign alu_src = 1'b0;
  assign branch = 1'b0;
  assign c_in = 1'b0;
  assign en = 1'b1;
  assign imm_in = 1'b0;
  assign imm_selctor = 2'b00;
  assign mem_read = 1'b0;
  assign mem_to_reg = 2'b10;
  assign mem_write = 1'b0;
  assign pc_next = 4'b0001;
  assign re_wr = 1'b1;
  assign regdest = 2'b10;
  assign rt___rd = 1'b0;
  assign set___sset = 1'b0;
  assign shift_select = 2'b00;
endmodule
